// Logisim project regfile.circ as structural Verilog: 1 circuit, main circuit main
module main (
  input  [4:0] rs1,
  input  [4:0] rs2,
  input  [4:0] rd,
  input  [31:0] Write_Data,
  input  RegWEn,
  input  clk,
  output [31:0] ra,
  output [31:0] sp,
  output [31:0] t0,
  output [31:0] t1,
  output [31:0] t2,
  output [31:0] s0,
  output [31:0] s1,
  output [31:0] a0,
  output [31:0] Read_Data_1,
  output [31:0] Read_Data_2
);

  wire write_en0, write_en1, write_en2, write_en5, write_en6, write_en7, write_en8, write_en9, write_en10;

  Demultiplexer #(.select(4), .enable("false")) demultiplexer_1 (
    .out0(write_en0), .out1(write_en1), .out2(write_en2), .out5(write_en5), .out6(write_en6),
    .out7(write_en7), .out8(write_en8), .out9(write_en9), .out10(write_en10), .in(RegWEn), .sel(rd[3:0]));  // open: out3, out4, out11, out12, out13, out14, out15
  Multiplexer #(.select(4), .width(32), .enable("false")) multiplexer_1 (
    .in0({32{1'b0}}), .in1(ra), .in2(sp), .in5(t0), .in6(t1), .in7(t2), .in8(s0), .in9(s1), .in10(a0),
    .out(Read_Data_1), .sel(rs1[3:0]));  // open: in3, in4, in11, in12, in13, in14, in15
  Multiplexer #(.select(4), .width(32), .enable("false")) multiplexer_2 (
    .in0({32{1'b0}}), .in1(ra), .in2(sp), .in5(t0), .in6(t1), .in7(t2), .in8(s0), .in9(s1), .in10(a0),
    .out(Read_Data_2), .sel(rs2[3:0]));  // open: in3, in4, in11, in12, in13, in14, in15
  Register #(.width(32)) x0 (.D({32{1'b0}}), .en(write_en0), .clk(clk));  // open: Q, clr
  Register #(.width(32)) x1 (.D(Write_Data), .en(write_en1), .clk(clk), .Q(ra));  // open: clr
  Register #(.width(32)) x2 (.D(Write_Data), .en(write_en2), .clk(clk), .Q(sp));  // open: clr
  Register #(.width(32)) x5 (.D(Write_Data), .en(write_en5), .clk(clk), .Q(t0));  // open: clr
  Register #(.width(32)) x6 (.D(Write_Data), .en(write_en6), .clk(clk), .Q(t1));  // open: clr
  Register #(.width(32)) x7 (.D(Write_Data), .en(write_en7), .clk(clk), .Q(t2));  // open: clr
  Register #(.width(32)) x8 (.D(Write_Data), .en(write_en8), .clk(clk), .Q(s0));  // open: clr
  Register #(.width(32)) x9 (.D(Write_Data), .en(write_en9), .clk(clk), .Q(s1));  // open: clr
  Register #(.width(32)) x10 (.D(Write_Data), .en(write_en10), .clk(clk), .Q(a0));  // open: clr

  // Other names for the same wires on the sheet: read_data1[31:0] = Read_Data_1; read_data2[31:0] = Read_Data_2;
  //   read_reg1[4:0] = rs1; reg1_read[3:0] = rs1[3:0]; read_reg2[4:0] = rs2; reg2_read[3:0] = rs2[3:0];
  //   write_en = RegWEn; write_reg[4:0] = rd

  // Notes on the sheet:
  //   INPUTS to your circuit
  //   DON'T CHANGE THE LOCATIONS OF THE INPUTS AND OUTPUTS!
  //   These are DEBUG/TEST outputs from your circuit.
  //   OUTPUTS from your circuit
endmodule
