// Logisim project alu.circ as structural Verilog: 18 circuits, main circuit alu
module alu (
  input  [31:0] A,
  input  [31:0] B,
  input  [3:0] ALUSel,
  output [31:0] Result
);

  wire [31:0] alu0, alu1, alu2, alu3, alu4, alu5, alu6, alu7, alu8, alu9, alu10, alu11, alu12, alu13, alu14,
       alu15;

  or_1 or_1_1 (.A(A), .B(B), .or_out(alu1));
  and_0 and_0_1 (.input_A(A), .input_B(B), .OUT_PUT(alu0));
  xor_2 xor_2_1 (.input_A(A), .input_B(B), .OUT_PUT(alu2));
  add_3 add_3_1 (.A(A), .B(B), .add_out(alu3));
  sub_4 sub_4_1 (.input_A(A), .input_B(B), .OUT_PUT(alu4));
  divu_8 divu_8_1 (.A(A), .B(B), .divu_out(alu8));
  div_9 div_9_1 (.A(A), .B(B), .div_out(alu9));
  remu_10 remu_10_1 (.A(A), .B(B), .remu_out(alu10));
  mulhu_6 mulhu_6_1 (.input_A(A), .input_B(B), .upper_32bits(alu6));
  mulh_7 mulh_7_1 (.input_A(A), .input_B(B), .MUL_OUT(alu5), .MUL_OUT_UPPER(alu7));
  srl_11 srl_11_1 (.A(A), .B(B), .srl_out(alu11));
  sra_12 sra_12_1 (.A(A), .B(B), .sra_out(alu12));
  slt_13 slt_13_1 (.A(A), .B(B), .slt_out(alu13));
  sir_14 sir_14_1 (.A(A), .B(B), .sir_out(alu14));
  Multiplexer #(.select(4), .width(32), .enable("false")) multiplexer_1 (
    .in0(alu0), .in1(alu1), .in2(alu2), .in3(alu3), .in4(alu4), .in5(alu5), .in6(alu6), .in7(alu7),
    .in8(alu8), .in9(alu9), .in10(alu10), .in11(alu11), .in12(alu12), .in13(alu13), .in14(alu14),
    .in15(alu15), .out(Result), .sel(ALUSel));
  sll_15 sll_15_1 (.A(A), .sll_out(alu15), .B(B));

  // Notes on the sheet:
  //   INPUTS to your circuit
  //   DON'T CHANGE THE LOCATIONS OF THE INPUTS AND OUTPUTS!
  //   OUTPUT from your circuit
endmodule

module and_0 (
  input  [31:0] input_A,
  input  [31:0] input_B,
  output [31:0] OUT_PUT
);

  assign OUT_PUT = input_A & input_B;  // AND_Gate and_1, 32 bits wide
endmodule

module or_1 (
  input  [31:0] A,
  input  [31:0] B,
  output [31:0] or_out
);

  assign or_out = A | B;  // OR_Gate or_1, 32 bits wide
endmodule

module xor_2 (
  input  [31:0] input_A,
  input  [31:0] input_B,
  output [31:0] OUT_PUT
);

  assign OUT_PUT = input_A ^ input_B;  // XOR_Gate xor_1, 32 bits wide
endmodule

module add_3 (
  input  [31:0] A,
  input  [31:0] B,
  output [31:0] add_out
);

  Adder #(.width(32)) adder_1 (.a(A), .b(B), .out(add_out));  // open: cin, cout
endmodule

module sub_4 (
  input  [31:0] input_A,
  input  [31:0] input_B,
  output [31:0] OUT_PUT
);

  Subtractor #(.width(32)) subtractor_1 (.a(input_A), .b(input_B), .out(OUT_PUT));  // open: bin, bout
endmodule

module negate (
  input  [31:0] in_1,
  output [31:0] out_2,
  output [31:0] Overflow
);

  wire adder_1_cout;
  wire [31:0] not_1_out;

  assign not_1_out = ~in_1;  // NOT_Gate not_1, 32 bits wide
  Adder #(.width(32)) adder_1 (.a(not_1_out), .b(32'h1), .out(out_2), .cout(adder_1_cout));  // open: cin
  assign Overflow = {{31{1'b0}}, adder_1_cout};  // Bit_Extender bit_extender_1
endmodule

module mulhu_6 (
  input  [31:0] input_A,
  input  [31:0] input_B,
  output [31:0] upper_32bits
);

  Multiplier #(.width(32)) multiplier_1 (.a(input_A), .b(input_B), .cout(upper_32bits));  // open: out, cin
endmodule

module mulh_7 (
  input  [31:0] input_A,
  input  [31:0] input_B,
  output [31:0] MUL_OUT,
  output [31:0] MUL_OUT_UPPER
);

  wire [31:0] adder_1_out, adder_2_out, multiplier_1_cout, multiplier_1_out, multiplier_2_cout,
       multiplier_2_out, multiplier_3_cout, multiplier_3_out, multiplier_4_cout, multiplier_4_out,
       negate_1_out_2, negate_1_overflow, negate_2_out_2, negate_2_overflow, negator_1_out, negator_2_out,
       negator_3_out, negator_4_out, not_1_out, not_2_out;

  Multiplier #(.width(32)) multiplier_1 (
    .a(input_A), .b(input_B), .out(multiplier_1_out), .cout(multiplier_1_cout));  // open: cin
  Negator #(.width(32)) negator_1 (.in(input_A), .out(negator_1_out));
  Negator #(.width(32)) negator_2 (.in(input_B), .out(negator_2_out));
  Negator #(.width(32)) negator_3 (.in(input_A), .out(negator_3_out));
  Negator #(.width(32)) negator_4 (.in(input_B), .out(negator_4_out));
  Multiplier #(.width(32)) multiplier_2 (
    .a(negator_1_out), .b(input_B), .out(multiplier_2_out), .cout(multiplier_2_cout));  // open: cin
  Multiplier #(.width(32)) multiplier_3 (
    .a(input_A), .b(negator_2_out), .out(multiplier_3_out), .cout(multiplier_3_cout));  // open: cin
  Multiplier #(.width(32)) multiplier_4 (
    .a(negator_3_out), .b(negator_4_out), .out(multiplier_4_out), .cout(multiplier_4_cout));  // open: cin
  negate negate_1 (.in_1(multiplier_2_out), .out_2(negate_1_out_2), .Overflow(negate_1_overflow));
  assign not_1_out = ~multiplier_2_cout;  // NOT_Gate not_1, 32 bits wide
  negate negate_2 (.in_1(multiplier_3_out), .out_2(negate_2_out_2), .Overflow(negate_2_overflow));
  assign not_2_out = ~multiplier_3_cout;  // NOT_Gate not_2, 32 bits wide
  Adder #(.width(32)) adder_1 (.a(negate_1_overflow), .b(not_1_out), .out(adder_1_out));  // open: cin, cout
  Adder #(.width(32)) adder_2 (.a(negate_2_overflow), .b(not_2_out), .out(adder_2_out));  // open: cin, cout
  Multiplexer #(.select(2), .width(32), .enable("false")) multiplexer_1 (
    .in0(multiplier_1_out), .in1(negate_1_out_2), .in2(negate_2_out_2), .in3(multiplier_4_out),
    .out(MUL_OUT), .sel({input_B[31], input_A[31]}));
  Multiplexer #(.select(2), .width(32), .enable("false")) multiplexer_2 (
    .in0(multiplier_1_cout), .in1(adder_1_out), .in2(adder_2_out), .in3(multiplier_4_cout),
    .out(MUL_OUT_UPPER), .sel({input_B[31], input_A[31]}));

  // Other names for the same wires on the sheet: A[31:0] = input_A; B[31:0] = input_B;
  //   mux[1:0] = {input_B[31], input_A[31]}
endmodule

module divu_8 (
  input  [31:0] A,
  input  [31:0] B,
  output [31:0] divu_out
);

  Divider #(.width(32)) divider_1 (.a(A), .b(B), .out(divu_out));  // open: upper, rem
endmodule

module div_9 (
  input  [31:0] A,
  input  [31:0] B,
  output [31:0] div_out
);

  wire [31:0] condition00, condition01, condition10, condition11, divider_2_out, divider_3_out,
       negate_1_out_2, negate_3_out_2, negate_4_out_2, negate_5_out_2;

  negate negate_1 (.in_1(A), .out_2(negate_1_out_2));  // open: Overflow
  Divider #(.width(32)) divider_1 (.a(A), .b(B), .out(condition00));  // open: upper, rem
  Divider #(.width(32)) divider_2 (.a(negate_1_out_2), .b(B), .out(divider_2_out));  // open: upper, rem
  negate negate_2 (.in_1(divider_2_out), .out_2(condition01));  // open: Overflow
  negate negate_3 (.in_1(B), .out_2(negate_3_out_2));  // open: Overflow
  negate negate_4 (.in_1(A), .out_2(negate_4_out_2));  // open: Overflow
  negate negate_5 (.in_1(B), .out_2(negate_5_out_2));  // open: Overflow
  // Probe on div_out
  Multiplexer #(.select(2), .width(32), .enable("false")) multiplexer_1 (
    .in0(condition00), .in1(condition01), .in2(condition10), .in3(condition11), .out(div_out),
    .sel({B[31], A[31]}));
  Divider #(.width(32)) divider_3 (.a(A), .b(negate_3_out_2), .out(divider_3_out));  // open: upper, rem
  Divider #(.width(32)) divider_4 (.a(negate_4_out_2), .b(negate_5_out_2), .out(condition11));  // open: upper, rem
  negate negate_6 (.in_1(divider_3_out), .out_2(condition10));  // open: Overflow

  // Other names for the same wires on the sheet: input_A[31:0] = A; input_B[31:0] = B
endmodule

module remu_10 (
  input  [31:0] A,
  input  [31:0] B,
  output [31:0] remu_out
);

  Divider #(.width(32)) divider_1 (.a(A), .b(B), .rem(remu_out));  // open: out, upper
endmodule

module srl_11 (
  input  [31:0] A,
  input  [31:0] B,
  output [31:0] srl_out
);

  wire comparator_1_gt;

  // Probe on comparator_1_gt
  Comparator #(.width(32), .mode("unsigned")) comparator_1 (.a(B), .b(32'h1f), .gt(comparator_1_gt));  // open: eq, lt
  Shifter #(.width(32), .shift("lr")) shifter_1 (.in(A), .\dist (B[4:0]), .out(srl_out));
  Multiplexer #(.width(32), .enable("false")) multiplexer_1 (
    .in0(srl_out), .in1({32{1'b0}}), .sel(comparator_1_gt));  // open: out
endmodule

module sra_12 (
  input  [31:0] A,
  input  [31:0] B,
  output [31:0] sra_out
);

  wire comparator_1_gt;
  wire [31:0] multiplexer_1_out;

  // Probe on comparator_1_gt
  Comparator #(.width(32), .mode("unsigned")) comparator_1 (.a(B), .b(32'h1f), .gt(comparator_1_gt));  // open: eq, lt
  Multiplexer #(.width(32), .enable("false")) multiplexer_1 (
    .in0({32{1'b0}}), .in1({32{1'b1}}), .out(multiplexer_1_out), .sel(A[31]));
  Shifter #(.width(32), .shift("ar")) shifter_1 (.in(A), .\dist (B[4:0]), .out(sra_out));
  Multiplexer #(.width(32), .enable("false")) multiplexer_2 (
    .in0(sra_out), .in1(multiplexer_1_out), .sel(comparator_1_gt));  // open: out
endmodule

module slt_13 (
  input  [31:0] A,
  input  [31:0] B,
  output [31:0] slt_out
);

  wire comparator_1_lt;

  Comparator #(.width(32)) comparator_1 (.a(A), .b(B), .lt(comparator_1_lt));  // open: gt, eq
  assign slt_out = {{31{1'b0}}, comparator_1_lt};  // Bit_Extender bit_extender_1
endmodule

module part_of_sir_8 (
  input  [7:0] in_1,
  input  [7:0] in_2,
  output out_3,
  output out_4,
  output out_5,
  output out_6,
  output out_7,
  output out_8,
  output out_9,
  output out_10
);

  Comparator #(.width(1), .mode("unsigned")) comparator_1 (.a(in_1[7]), .b(in_2[0]), .eq(out_3));  // open: gt, lt
  Comparator #(.width(1), .mode("unsigned")) comparator_2 (.a(in_1[6]), .b(in_2[1]), .eq(out_4));  // open: gt, lt
  Comparator #(.width(1), .mode("unsigned")) comparator_3 (.a(in_1[5]), .b(in_2[2]), .eq(out_5));  // open: gt, lt
  Comparator #(.width(1), .mode("unsigned")) comparator_4 (.a(in_1[4]), .b(in_2[3]), .eq(out_6));  // open: gt, lt
  Comparator #(.width(1), .mode("unsigned")) comparator_5 (.a(in_1[3]), .b(in_2[4]), .eq(out_7));  // open: gt, lt
  Comparator #(.width(1), .mode("unsigned")) comparator_6 (.a(in_1[2]), .b(in_2[5]), .eq(out_8));  // open: gt, lt
  Comparator #(.width(1), .mode("unsigned")) comparator_7 (.a(in_1[1]), .b(in_2[6]), .eq(out_9));  // open: gt, lt
  Comparator #(.width(1), .mode("unsigned")) comparator_8 (.a(in_1[0]), .b(in_2[7]), .eq(out_10));  // open: gt, lt
endmodule

module sir_14 (
  input  [31:0] A,
  input  [31:0] B,
  output [31:0] sir_out
);

  wire and_1_out, and_2_out, and_3_out, and_4_out, and_5_out, part_of_sir_8_1_out_3, part_of_sir_8_1_out_4,
       part_of_sir_8_1_out_5, part_of_sir_8_1_out_6, part_of_sir_8_1_out_7, part_of_sir_8_1_out_8,
       part_of_sir_8_1_out_9, part_of_sir_8_1_out_10, part_of_sir_8_2_out_3, part_of_sir_8_2_out_4,
       part_of_sir_8_2_out_5, part_of_sir_8_2_out_6, part_of_sir_8_2_out_7, part_of_sir_8_2_out_8,
       part_of_sir_8_2_out_9, part_of_sir_8_2_out_10, part_of_sir_8_3_out_3, part_of_sir_8_3_out_4,
       part_of_sir_8_3_out_5, part_of_sir_8_3_out_6, part_of_sir_8_3_out_7, part_of_sir_8_3_out_8,
       part_of_sir_8_3_out_9, part_of_sir_8_3_out_10, part_of_sir_8_4_out_3, part_of_sir_8_4_out_4,
       part_of_sir_8_4_out_5, part_of_sir_8_4_out_6, part_of_sir_8_4_out_7, part_of_sir_8_4_out_8,
       part_of_sir_8_4_out_9, part_of_sir_8_4_out_10;

  part_of_sir_8 part_of_sir_8_1 (
    .in_1(A[31:24]), .in_2(B[7:0]), .out_3(part_of_sir_8_1_out_3), .out_4(part_of_sir_8_1_out_4),
    .out_5(part_of_sir_8_1_out_5), .out_6(part_of_sir_8_1_out_6), .out_7(part_of_sir_8_1_out_7),
    .out_8(part_of_sir_8_1_out_8), .out_9(part_of_sir_8_1_out_9), .out_10(part_of_sir_8_1_out_10));
  part_of_sir_8 part_of_sir_8_2 (
    .in_1(A[23:16]), .in_2(B[15:8]), .out_3(part_of_sir_8_2_out_3), .out_4(part_of_sir_8_2_out_4),
    .out_5(part_of_sir_8_2_out_5), .out_6(part_of_sir_8_2_out_6), .out_7(part_of_sir_8_2_out_7),
    .out_8(part_of_sir_8_2_out_8), .out_9(part_of_sir_8_2_out_9), .out_10(part_of_sir_8_2_out_10));
  part_of_sir_8 part_of_sir_8_3 (
    .in_1(A[15:8]), .in_2(B[23:16]), .out_3(part_of_sir_8_3_out_3), .out_4(part_of_sir_8_3_out_4),
    .out_5(part_of_sir_8_3_out_5), .out_6(part_of_sir_8_3_out_6), .out_7(part_of_sir_8_3_out_7),
    .out_8(part_of_sir_8_3_out_8), .out_9(part_of_sir_8_3_out_9), .out_10(part_of_sir_8_3_out_10));
  part_of_sir_8 part_of_sir_8_4 (
    .in_1(A[7:0]), .in_2(B[31:24]), .out_3(part_of_sir_8_4_out_3), .out_4(part_of_sir_8_4_out_4),
    .out_5(part_of_sir_8_4_out_5), .out_6(part_of_sir_8_4_out_6), .out_7(part_of_sir_8_4_out_7),
    .out_8(part_of_sir_8_4_out_8), .out_9(part_of_sir_8_4_out_9), .out_10(part_of_sir_8_4_out_10));
  and and_1 (and_1_out, part_of_sir_8_1_out_3, part_of_sir_8_1_out_4, part_of_sir_8_1_out_5, part_of_sir_8_1_out_6, part_of_sir_8_1_out_7, part_of_sir_8_1_out_8, part_of_sir_8_1_out_9, part_of_sir_8_1_out_10);
  and and_2 (and_2_out, part_of_sir_8_2_out_3, part_of_sir_8_2_out_4, part_of_sir_8_2_out_5, part_of_sir_8_2_out_6, part_of_sir_8_2_out_7, part_of_sir_8_2_out_8, part_of_sir_8_2_out_9, part_of_sir_8_2_out_10);
  and and_3 (and_3_out, part_of_sir_8_3_out_3, part_of_sir_8_3_out_4, part_of_sir_8_3_out_5, part_of_sir_8_3_out_6, part_of_sir_8_3_out_7, part_of_sir_8_3_out_8, part_of_sir_8_3_out_9, part_of_sir_8_3_out_10);
  and and_4 (and_4_out, part_of_sir_8_4_out_3, part_of_sir_8_4_out_4, part_of_sir_8_4_out_5, part_of_sir_8_4_out_6, part_of_sir_8_4_out_7, part_of_sir_8_4_out_8, part_of_sir_8_4_out_9, part_of_sir_8_4_out_10);
  and and_5 (and_5_out, and_1_out, and_2_out, and_3_out, and_4_out);
  assign sir_out = {{31{1'b0}}, and_5_out};  // Bit_Extender bit_extender_1

  // Other names for the same wires on the sheet: A_7_0[7:0] = A[7:0]; A_15_8[7:0] = A[15:8]; A_23_16[7:0] = A[23:16];
  //   A_31_24[7:0] = A[31:24]; B_7_0[7:0] = B[7:0]; B_15_8[7:0] = B[15:8]; B_23_16[7:0] = B[23:16];
  //   B_31_24[7:0] = B[31:24]
endmodule

module sll_15 (
  input  [31:0] A,
  input  [31:0] B,
  output [31:0] sll_out
);

  wire comparator_1_gt;

  // Probe on comparator_1_gt
  Comparator #(.width(32), .mode("unsigned")) comparator_1 (.a(B), .b(32'h1f), .gt(comparator_1_gt));  // open: eq, lt
  Shifter #(.width(32)) shifter_1 (.in(A), .\dist (B[4:0]), .out(sll_out));
  Multiplexer #(.width(32), .enable("false")) multiplexer_1 (
    .in0(sll_out), .in1({32{1'b0}}), .sel(comparator_1_gt));  // open: out
endmodule
