// Logisim project cpu.circ as structural Verilog: 4 circuits, main circuit main
module main (
  input  [31:0] INSTRUCTION,
  input  CLOCK,
  output [31:0] FETCH_ADDRESS,
  output [31:0] ra,
  output [31:0] sp,
  output [31:0] t0,
  output [31:0] t1,
  output [31:0] t2,
  output [31:0] s0,
  output [31:0] s1,
  output [31:0] a0
);

  wire BrEq, BrLT, BrUn, BSel, comparator_1_lt, comparator_2_lt, PCSel, RegWEn;
  wire [1:0] ASel, WBSel;
  wire [2:0] ImmSel, MemRW;
  wire [3:0] ALUSel;
  wire [31:0] adder_2_out, ALU_result, DataA, DataB, DMEM_result, imm31_0, INSTRUCTION_real,
       multiplexer_1_out, multiplexer_2_out, multiplexer_3_out, multiplexer_5_out, PC, PC_ADD_4, PC_q, WB;

  Multiplexer #(.width(32), .enable("false")) multiplexer_1 (
    .in0(PC_ADD_4), .in1(ALU_result), .out(multiplexer_1_out), .sel(PCSel));
  Register #(.width(32)) u_PC (.D(multiplexer_1_out), .clk(CLOCK), .Q(PC_q));  // open: en, clr
  // Probe on INSTRUCTION_real
  Adder #(.width(32)) adder_1 (.a(32'h4), .b(PC_q), .out(PC_ADD_4));  // open: cin, cout
  Shifter #(.width(32), .shift("lr")) shifter_1 (.in(PC_q), .\dist (5'b00010), .out(FETCH_ADDRESS));
  // Probe on multiplexer_2_out
  Multiplexer #(.width(32), .enable("false")) multiplexer_2 (
    .in0(INSTRUCTION), .in1(32'h13), .out(multiplexer_2_out), .sel(PCSel));
  Register #(.width(32)) register_1 (.D(PC_q), .clk(CLOCK), .Q(PC));  // open: en, clr
  control Control_logic (
    .BrEq(BrEq), .ALUSel(ALUSel), .BrLT(BrLT), .BSel(BSel), .ImmSel(ImmSel), .ASel(ASel), .PCSel(PCSel),
    .BrUn(BrUn), .Inst(INSTRUCTION_real), .MemRW(MemRW), .RegWEn(RegWEn), .WBSel(WBSel));
  // Probe on WBSel
  Register #(.width(32)) register_2 (.D(multiplexer_2_out), .clk(CLOCK), .Q(INSTRUCTION_real));  // open: en, clr
  // Probe on ImmSel
  // Probe on ASel
  // Probe on ALUSel
  // Probe on MemRW
  imm Imm_GEN (.Imm(imm31_0), .ImmSel(ImmSel), .Inst31to7(INSTRUCTION_real[31:7]));
  regfile_main RegFile (
    .rs2(INSTRUCTION_real[24:20]), .rd(INSTRUCTION_real[11:7]), .Read_Data_1(DataA), .Read_Data_2(DataB),
    .ra(ra), .sp(sp), .t0(t0), .t1(t1), .t2(t2), .s0(s0), .s1(s1), .a0(a0), .rs1(INSTRUCTION_real[19:15]),
    .Write_Data(WB), .RegWEn(RegWEn), .clk(CLOCK));
  Comparator #(.width(32)) comparator_1 (.a(DataA), .b(DataB), .eq(BrEq), .lt(comparator_1_lt));  // open: gt
  Comparator #(.width(32), .mode("unsigned")) comparator_2 (
    .a(DataA), .b(DataB), .lt(comparator_2_lt));  // open: gt, eq
  // Probe on multiplexer_5_out
  Multiplexer #(.width(32), .enable("false")) multiplexer_3 (
    .in0(DataB), .in1(imm31_0), .out(multiplexer_3_out), .sel(BSel));
  Multiplexer #(.enable("false")) multiplexer_4 (.in0(comparator_1_lt), .in1(comparator_2_lt), .out(BrLT), .sel(BrUn));
  Multiplexer #(.select(2), .width(32), .enable("false")) multiplexer_5 (
    .in0(DataA), .in1(PC), .in2({32{1'b0}}), .out(multiplexer_5_out), .sel(ASel));  // open: in3
  // Probe on multiplexer_3_out
  // Probe on ALU_result
  alu Arithmetic_Logic_Unit (.A(multiplexer_5_out), .B(multiplexer_3_out), .ALUSel(ALUSel), .Result(ALU_result));
  mem_main DMEM (.WriteAddr(ALU_result), .WriteData(DataB), .MemRW(MemRW), .ReadData(DMEM_result), .clk(CLOCK));
  Adder #(.width(32)) adder_2 (.a(PC), .b(32'h4), .out(adder_2_out));  // open: cin, cout
  Multiplexer #(.select(2), .width(32), .enable("false")) multiplexer_6 (
    .in0(DMEM_result), .in1(ALU_result), .in2(adder_2_out), .out(WB), .sel(WBSel));  // open: in3

  // Other names for the same wires on the sheet: clk = CLOCK; fetch_addr[31:0] = FETCH_ADDRESS

  // Notes on the sheet:
  //   Output
  //   Inputs/Outputs from run.circ. DO NOT MOVE THESE.
  //   Inputs
  //   Inputs/Outputs from run.circ. DO NOT MOVE THESE.
endmodule

module control (
  input  [31:0] Inst,
  input  BrEq,
  input  BrLT,
  output [2:0] ImmSel,
  output PCSel,
  output [1:0] ASel,
  output BSel,
  output [3:0] ALUSel,
  output [2:0] MemRW,
  output RegWEn,
  output [1:0] WBSel,
  output BrUn
);

  wire and_1_out, and_2_out, and_3_out, and_4_out, and_5_out, and_6_out, and_7_out, and_8_out, and_9_out,
       and_10_out, and_11_out, and_12_out, and_13_out, and_14_out, and_15_out, and_16_out, and_17_out,
       and_18_out, and_19_out, and_20_out, and_21_out, and_22_out, and_23_out, and_24_out, and_25_out,
       and_26_out, and_27_out, and_28_out, and_29_out, and_30_out, and_31_out, and_32_out, and_33_out,
       and_34_out, and_35_out, and_36_out, and_37_out, comparator_1_eq, comparator_2_eq, comparator_3_eq,
       comparator_4_eq, comparator_5_eq, comparator_6_eq, comparator_7_eq, comparator_8_eq, comparator_9_eq,
       comparator_10_eq, comparator_11_eq, comparator_12_eq, comparator_13_eq, comparator_14_eq,
       comparator_15_eq, comparator_16_eq, comparator_17_eq, comparator_18_eq, comparator_19_eq,
       comparator_20_eq, comparator_21_eq, comparator_22_eq, comparator_23_eq, comparator_24_eq,
       comparator_25_eq, comparator_26_eq, comparator_27_eq, comparator_28_eq, comparator_29_eq,
       comparator_30_eq, comparator_31_eq, comparator_32_eq, comparator_33_eq, comparator_34_eq,
       comparator_35_eq, comparator_36_eq, comparator_37_eq, comparator_38_eq, comparator_39_eq,
       comparator_40_eq, comparator_41_eq, comparator_42_eq, comparator_43_eq, comparator_44_eq,
       comparator_45_eq, comparator_46_eq, comparator_47_eq, comparator_48_eq, comparator_49_eq,
       comparator_50_eq, comparator_51_eq, comparator_52_eq, comparator_53_eq, comparator_54_eq,
       comparator_55_eq, comparator_56_eq, comparator_57_eq, comparator_58_eq, comparator_59_eq,
       comparator_60_eq, comparator_61_eq, comparator_62_eq, comparator_63_eq, comparator_64_eq,
       comparator_65_eq, comparator_66_eq, comparator_67_eq, comparator_68_eq, comparator_69_eq,
       comparator_70_eq, comparator_71_eq, comparator_72_eq, comparator_73_eq, comparator_74_eq,
       comparator_75_eq, comparator_76_eq, comparator_77_eq, comparator_78_eq, comparator_79_eq,
       comparator_80_eq, comparator_81_eq, comparator_82_eq, comparator_83_eq, comparator_84_eq,
       comparator_85_eq, comparator_86_eq, comparator_87_eq, comparator_88_eq, comparator_89_eq,
       comparator_90_eq, comparator_91_eq, comparator_92_eq, comparator_93_eq, comparator_94_eq, not_1_out,
       not_2_out, not_3_out, not_4_out;
  wire [5:0] multiplexer_1_out, multiplexer_2_out, multiplexer_3_out, multiplexer_4_out, multiplexer_5_out,
       multiplexer_6_out, multiplexer_7_out, multiplexer_8_out, multiplexer_9_out, multiplexer_10_out,
       multiplexer_11_out, multiplexer_12_out, multiplexer_13_out, multiplexer_14_out, multiplexer_15_out,
       multiplexer_16_out, multiplexer_17_out, multiplexer_18_out, multiplexer_19_out, multiplexer_20_out,
       multiplexer_21_out, multiplexer_22_out, multiplexer_23_out, multiplexer_24_out, multiplexer_25_out,
       multiplexer_26_out, multiplexer_27_out, multiplexer_28_out, multiplexer_29_out, multiplexer_30_out,
       multiplexer_31_out, multiplexer_32_out, multiplexer_33_out, multiplexer_34_out, multiplexer_35_out,
       multiplexer_36_out, multiplexer_37_out, multiplexer_38_out, multiplexer_39_out, multiplexer_40_out,
       or_1_out, or_2_out, or_3_out;
  wire [13:13] rom_1_data;

  Comparator #(.width(7), .mode("unsigned")) comparator_1 (
    .a(Inst[6:0]), .b(7'b0110011), .eq(comparator_1_eq));  // open: gt, lt
  Comparator #(.width(3), .mode("unsigned")) comparator_2 (
    .a(Inst[14:12]), .b(3'b000), .eq(comparator_2_eq));  // open: gt, lt
  Comparator #(.width(7), .mode("unsigned")) comparator_3 (
    .a(Inst[31:25]), .b({7{1'b0}}), .eq(comparator_3_eq));  // open: gt, lt
  Comparator #(.width(7), .mode("unsigned")) comparator_4 (
    .a(Inst[6:0]), .b(7'b0110011), .eq(comparator_4_eq));  // open: gt, lt
  Comparator #(.width(3), .mode("unsigned")) comparator_5 (
    .a(Inst[14:12]), .b(3'b000), .eq(comparator_5_eq));  // open: gt, lt
  Comparator #(.width(7), .mode("unsigned")) comparator_6 (
    .a(Inst[31:25]), .b(7'b0000001), .eq(comparator_6_eq));  // open: gt, lt
  Comparator #(.width(7), .mode("unsigned")) comparator_7 (
    .a(Inst[6:0]), .b(7'b0110011), .eq(comparator_7_eq));  // open: gt, lt
  Comparator #(.width(3), .mode("unsigned")) comparator_8 (
    .a(Inst[14:12]), .b(3'b000), .eq(comparator_8_eq));  // open: gt, lt
  Comparator #(.width(7), .mode("unsigned")) comparator_9 (
    .a(Inst[31:25]), .b(7'b0100000), .eq(comparator_9_eq));  // open: gt, lt
  Comparator #(.width(7), .mode("unsigned")) comparator_10 (
    .a(Inst[6:0]), .b(7'b0110011), .eq(comparator_10_eq));  // open: gt, lt
  Comparator #(.width(3), .mode("unsigned")) comparator_11 (
    .a(Inst[14:12]), .b(3'b001), .eq(comparator_11_eq));  // open: gt, lt
  Comparator #(.width(7), .mode("unsigned")) comparator_12 (
    .a(Inst[31:25]), .b({7{1'b0}}), .eq(comparator_12_eq));  // open: gt, lt
  Comparator #(.width(7), .mode("unsigned")) comparator_13 (
    .a(Inst[6:0]), .b(7'b0110011), .eq(comparator_13_eq));  // open: gt, lt
  Comparator #(.width(3), .mode("unsigned")) comparator_14 (
    .a(Inst[14:12]), .b(3'b001), .eq(comparator_14_eq));  // open: gt, lt
  Comparator #(.width(7), .mode("unsigned")) comparator_15 (
    .a(Inst[31:25]), .b(7'b0000001), .eq(comparator_15_eq));  // open: gt, lt
  Comparator #(.width(7), .mode("unsigned")) comparator_16 (
    .a(Inst[6:0]), .b(7'b0110011), .eq(comparator_16_eq));  // open: gt, lt
  Comparator #(.width(3), .mode("unsigned")) comparator_17 (
    .a(Inst[14:12]), .b(3'b011), .eq(comparator_17_eq));  // open: gt, lt
  Comparator #(.width(7), .mode("unsigned")) comparator_18 (
    .a(Inst[31:25]), .b(7'b0000001), .eq(comparator_18_eq));  // open: gt, lt
  Comparator #(.width(7), .mode("unsigned")) comparator_19 (
    .a(Inst[6:0]), .b(7'b0110011), .eq(comparator_19_eq));  // open: gt, lt
  Comparator #(.width(3), .mode("unsigned")) comparator_20 (
    .a(Inst[14:12]), .b(3'b100), .eq(comparator_20_eq));  // open: gt, lt
  Comparator #(.width(7), .mode("unsigned")) comparator_21 (
    .a(Inst[31:25]), .b({7{1'b0}}), .eq(comparator_21_eq));  // open: gt, lt
  Comparator #(.width(7), .mode("unsigned")) comparator_22 (
    .a(Inst[6:0]), .b(7'b0110011), .eq(comparator_22_eq));  // open: gt, lt
  Comparator #(.width(3), .mode("unsigned")) comparator_23 (
    .a(Inst[14:12]), .b(3'b100), .eq(comparator_23_eq));  // open: gt, lt
  Comparator #(.width(7), .mode("unsigned")) comparator_24 (
    .a(Inst[31:25]), .b(7'b0000001), .eq(comparator_24_eq));  // open: gt, lt
  Comparator #(.width(7), .mode("unsigned")) comparator_25 (
    .a(Inst[6:0]), .b(7'b0110011), .eq(comparator_25_eq));  // open: gt, lt
  Comparator #(.width(3), .mode("unsigned")) comparator_26 (
    .a(Inst[14:12]), .b(3'b101), .eq(comparator_26_eq));  // open: gt, lt
  Comparator #(.width(7), .mode("unsigned")) comparator_27 (
    .a(Inst[31:25]), .b(7'b0000001), .eq(comparator_27_eq));  // open: gt, lt
  Comparator #(.width(7), .mode("unsigned")) comparator_28 (
    .a(Inst[6:0]), .b(7'b0110011), .eq(comparator_28_eq));  // open: gt, lt
  Comparator #(.width(3), .mode("unsigned")) comparator_29 (
    .a(Inst[14:12]), .b(3'b101), .eq(comparator_29_eq));  // open: gt, lt
  Comparator #(.width(7), .mode("unsigned")) comparator_30 (
    .a(Inst[31:25]), .b({7{1'b0}}), .eq(comparator_30_eq));  // open: gt, lt
  Comparator #(.width(7), .mode("unsigned")) comparator_31 (
    .a(Inst[6:0]), .b(7'b0110011), .eq(comparator_31_eq));  // open: gt, lt
  Comparator #(.width(3), .mode("unsigned")) comparator_32 (
    .a(Inst[14:12]), .b(3'b110), .eq(comparator_32_eq));  // open: gt, lt
  Comparator #(.width(7), .mode("unsigned")) comparator_33 (
    .a(Inst[31:25]), .b({7{1'b0}}), .eq(comparator_33_eq));  // open: gt, lt
  Comparator #(.width(7), .mode("unsigned")) comparator_34 (
    .a(Inst[6:0]), .b(7'b0110011), .eq(comparator_34_eq));  // open: gt, lt
  Comparator #(.width(3), .mode("unsigned")) comparator_35 (
    .a(Inst[14:12]), .b(3'b111), .eq(comparator_35_eq));  // open: gt, lt
  Comparator #(.width(7), .mode("unsigned")) comparator_36 (
    .a(Inst[31:25]), .b(7'b0000001), .eq(comparator_36_eq));  // open: gt, lt
  Comparator #(.width(7), .mode("unsigned")) comparator_37 (
    .a(Inst[6:0]), .b(7'b0110011), .eq(comparator_37_eq));  // open: gt, lt
  Comparator #(.width(3), .mode("unsigned")) comparator_38 (
    .a(Inst[14:12]), .b(3'b111), .eq(comparator_38_eq));  // open: gt, lt
  Comparator #(.width(7), .mode("unsigned")) comparator_39 (
    .a(Inst[31:25]), .b({7{1'b0}}), .eq(comparator_39_eq));  // open: gt, lt
  // Probe on Inst[6:0]
  and and_1 (and_1_out, comparator_1_eq, comparator_2_eq, comparator_3_eq);
  and and_2 (and_2_out, comparator_4_eq, comparator_5_eq, comparator_6_eq);
  and and_3 (and_3_out, comparator_7_eq, comparator_8_eq, comparator_9_eq);
  and and_4 (and_4_out, comparator_10_eq, comparator_11_eq, comparator_12_eq);
  and and_5 (and_5_out, comparator_13_eq, comparator_14_eq, comparator_15_eq);
  and and_6 (and_6_out, comparator_16_eq, comparator_17_eq, comparator_18_eq);
  and and_7 (and_7_out, comparator_19_eq, comparator_20_eq, comparator_21_eq);
  and and_8 (and_8_out, comparator_22_eq, comparator_23_eq, comparator_24_eq);
  and and_9 (and_9_out, comparator_25_eq, comparator_26_eq, comparator_27_eq);
  and and_10 (and_10_out, comparator_28_eq, comparator_29_eq, comparator_30_eq);
  and and_11 (and_11_out, comparator_31_eq, comparator_32_eq, comparator_33_eq);
  and and_12 (and_12_out, comparator_34_eq, comparator_35_eq, comparator_36_eq);
  and and_13 (and_13_out, comparator_37_eq, comparator_38_eq, comparator_39_eq);
  Multiplexer #(.width(6), .enable("false")) multiplexer_1 (
    .in0({6{1'b0}}), .in1(6'b000001), .out(multiplexer_1_out), .sel(and_1_out));
  Multiplexer #(.width(6), .enable("false")) multiplexer_2 (
    .in0({6{1'b0}}), .in1(6'b000010), .out(multiplexer_2_out), .sel(and_2_out));
  Multiplexer #(.width(6), .enable("false")) multiplexer_3 (
    .in0({6{1'b0}}), .in1(6'b000011), .out(multiplexer_3_out), .sel(and_3_out));
  Multiplexer #(.width(6), .enable("false")) multiplexer_4 (
    .in0({6{1'b0}}), .in1(6'b000100), .out(multiplexer_4_out), .sel(and_4_out));
  Multiplexer #(.width(6), .enable("false")) multiplexer_5 (
    .in0({6{1'b0}}), .in1(6'b000101), .out(multiplexer_5_out), .sel(and_5_out));
  Multiplexer #(.width(6), .enable("false")) multiplexer_6 (
    .in0({6{1'b0}}), .in1(6'b000110), .out(multiplexer_6_out), .sel(and_6_out));
  Multiplexer #(.width(6), .enable("false")) multiplexer_7 (
    .in0({6{1'b0}}), .in1(6'b000111), .out(multiplexer_7_out), .sel(and_7_out));
  Multiplexer #(.width(6), .enable("false")) multiplexer_8 (
    .in0({6{1'b0}}), .in1(6'b001000), .out(multiplexer_8_out), .sel(and_8_out));
  Multiplexer #(.width(6), .enable("false")) multiplexer_9 (
    .in0({6{1'b0}}), .in1(6'b001001), .out(multiplexer_9_out), .sel(and_9_out));
  Multiplexer #(.width(6), .enable("false")) multiplexer_10 (
    .in0({6{1'b0}}), .in1(6'b001010), .out(multiplexer_10_out), .sel(and_10_out));
  Multiplexer #(.width(6), .enable("false")) multiplexer_11 (
    .in0({6{1'b0}}), .in1(6'b001011), .out(multiplexer_11_out), .sel(and_11_out));
  Multiplexer #(.width(6), .enable("false")) multiplexer_12 (
    .in0({6{1'b0}}), .in1(6'b001100), .out(multiplexer_12_out), .sel(and_12_out));
  Multiplexer #(.width(6), .enable("false")) multiplexer_13 (
    .in0({6{1'b0}}), .in1(6'b001101), .out(multiplexer_13_out), .sel(and_13_out));
  assign or_1_out = multiplexer_1_out | multiplexer_2_out | multiplexer_3_out | multiplexer_4_out | multiplexer_5_out | multiplexer_6_out | multiplexer_7_out | multiplexer_8_out | multiplexer_9_out | multiplexer_10_out | multiplexer_11_out | multiplexer_12_out | multiplexer_13_out | multiplexer_14_out | multiplexer_15_out | multiplexer_16_out | multiplexer_17_out | multiplexer_18_out | multiplexer_19_out | multiplexer_20_out | multiplexer_21_out | multiplexer_22_out | multiplexer_23_out | multiplexer_24_out | multiplexer_25_out | multiplexer_26_out | multiplexer_27_out | multiplexer_28_out | multiplexer_29_out | multiplexer_30_out | multiplexer_31_out | multiplexer_32_out;  // OR_Gate or_1, 6 bits wide
  assign or_2_out = multiplexer_34_out | multiplexer_38_out | multiplexer_33_out | multiplexer_36_out | multiplexer_37_out | multiplexer_35_out | multiplexer_40_out | multiplexer_39_out;  // OR_Gate or_2, 6 bits wide
  Comparator #(.width(7), .mode("unsigned")) comparator_40 (
    .a(Inst[6:0]), .b(7'b0000011), .eq(comparator_40_eq));  // open: gt, lt
  Comparator #(.width(3), .mode("unsigned")) comparator_41 (
    .a(Inst[14:12]), .b(3'b000), .eq(comparator_41_eq));  // open: gt, lt
  Comparator #(.width(7), .mode("unsigned")) comparator_42 (
    .a(Inst[6:0]), .b(7'b0000011), .eq(comparator_42_eq));  // open: gt, lt
  Comparator #(.width(3), .mode("unsigned")) comparator_43 (
    .a(Inst[14:12]), .b(3'b001), .eq(comparator_43_eq));  // open: gt, lt
  Comparator #(.width(7), .mode("unsigned")) comparator_44 (
    .a(Inst[6:0]), .b(7'b0000011), .eq(comparator_44_eq));  // open: gt, lt
  Comparator #(.width(3), .mode("unsigned")) comparator_45 (
    .a(Inst[14:12]), .b(3'b010), .eq(comparator_45_eq));  // open: gt, lt
  Comparator #(.width(7), .mode("unsigned")) comparator_46 (
    .a(Inst[6:0]), .b(7'b0000011), .eq(comparator_46_eq));  // open: gt, lt
  Comparator #(.width(3), .mode("unsigned")) comparator_47 (
    .a(Inst[14:12]), .b(3'b100), .eq(comparator_47_eq));  // open: gt, lt
  Comparator #(.width(7), .mode("unsigned")) comparator_48 (
    .a(Inst[6:0]), .b(7'b0000011), .eq(comparator_48_eq));  // open: gt, lt
  Comparator #(.width(3), .mode("unsigned")) comparator_49 (
    .a(Inst[14:12]), .b(3'b101), .eq(comparator_49_eq));  // open: gt, lt
  Comparator #(.width(7), .mode("unsigned")) comparator_50 (
    .a(Inst[6:0]), .b(7'b0010011), .eq(comparator_50_eq));  // open: gt, lt
  Comparator #(.width(3), .mode("unsigned")) comparator_51 (
    .a(Inst[14:12]), .b(3'b000), .eq(comparator_51_eq));  // open: gt, lt
  Comparator #(.width(7), .mode("unsigned")) comparator_52 (
    .a(Inst[6:0]), .b(7'b0010011), .eq(comparator_52_eq));  // open: gt, lt
  Comparator #(.width(3), .mode("unsigned")) comparator_53 (
    .a(Inst[14:12]), .b(3'b001), .eq(comparator_53_eq));  // open: gt, lt
  Comparator #(.width(7), .mode("unsigned")) comparator_54 (
    .a(Inst[31:25]), .b({7{1'b0}}), .eq(comparator_54_eq));  // open: gt, lt
  Comparator #(.width(7), .mode("unsigned")) comparator_55 (
    .a(Inst[6:0]), .b(7'b0010011), .eq(comparator_55_eq));  // open: gt, lt
  Comparator #(.width(3), .mode("unsigned")) comparator_56 (
    .a(Inst[14:12]), .b(3'b010), .eq(comparator_56_eq));  // open: gt, lt
  Comparator #(.width(7), .mode("unsigned")) comparator_57 (
    .a(Inst[6:0]), .b(7'b0010011), .eq(comparator_57_eq));  // open: gt, lt
  Comparator #(.width(3), .mode("unsigned")) comparator_58 (
    .a(Inst[14:12]), .b(3'b100), .eq(comparator_58_eq));  // open: gt, lt
  Comparator #(.width(7), .mode("unsigned")) comparator_59 (
    .a(Inst[6:0]), .b(7'b0010011), .eq(comparator_59_eq));  // open: gt, lt
  Comparator #(.width(3), .mode("unsigned")) comparator_60 (
    .a(Inst[14:12]), .b(3'b101), .eq(comparator_60_eq));  // open: gt, lt
  Comparator #(.width(7), .mode("unsigned")) comparator_61 (
    .a(Inst[31:25]), .b({7{1'b0}}), .eq(comparator_61_eq));  // open: gt, lt
  Comparator #(.width(7), .mode("unsigned")) comparator_62 (
    .a(Inst[6:0]), .b(7'b0010011), .eq(comparator_62_eq));  // open: gt, lt
  Comparator #(.width(3), .mode("unsigned")) comparator_63 (
    .a(Inst[14:12]), .b(3'b110), .eq(comparator_63_eq));  // open: gt, lt
  Comparator #(.width(7), .mode("unsigned")) comparator_64 (
    .a(Inst[6:0]), .b(7'b0010011), .eq(comparator_64_eq));  // open: gt, lt
  Comparator #(.width(3), .mode("unsigned")) comparator_65 (
    .a(Inst[14:12]), .b(3'b111), .eq(comparator_65_eq));  // open: gt, lt
  // Probe on or_3_out
  Multiplexer #(.width(6), .enable("false")) multiplexer_14 (
    .in0({6{1'b0}}), .in1(6'b001110), .out(multiplexer_14_out), .sel(and_14_out));
  and and_14 (and_14_out, comparator_40_eq, comparator_41_eq);
  Multiplexer #(.width(6), .enable("false")) multiplexer_15 (
    .in0({6{1'b0}}), .in1(6'b001111), .out(multiplexer_15_out), .sel(and_15_out));
  and and_15 (and_15_out, comparator_42_eq, comparator_43_eq);
  Multiplexer #(.width(6), .enable("false")) multiplexer_16 (
    .in0({6{1'b0}}), .in1(6'b010000), .out(multiplexer_16_out), .sel(and_16_out));
  and and_16 (and_16_out, comparator_44_eq, comparator_45_eq);
  Multiplexer #(.width(6), .enable("false")) multiplexer_17 (
    .in0({6{1'b0}}), .in1(6'b010001), .out(multiplexer_17_out), .sel(and_17_out));
  and and_17 (and_17_out, comparator_46_eq, comparator_47_eq);
  Multiplexer #(.width(6), .enable("false")) multiplexer_18 (
    .in0({6{1'b0}}), .in1(6'b010010), .out(multiplexer_18_out), .sel(and_18_out));
  and and_18 (and_18_out, comparator_48_eq, comparator_49_eq);
  Multiplexer #(.width(6), .enable("false")) multiplexer_19 (
    .in0({6{1'b0}}), .in1(6'b010011), .out(multiplexer_19_out), .sel(and_19_out));
  and and_19 (and_19_out, comparator_50_eq, comparator_51_eq);
  Multiplexer #(.width(6), .enable("false")) multiplexer_20 (
    .in0({6{1'b0}}), .in1(6'b010100), .out(multiplexer_20_out), .sel(and_20_out));
  and and_20 (and_20_out, comparator_52_eq, comparator_53_eq, comparator_54_eq);
  Multiplexer #(.width(6), .enable("false")) multiplexer_21 (
    .in0({6{1'b0}}), .in1(6'b010101), .out(multiplexer_21_out), .sel(and_21_out));
  and and_21 (and_21_out, comparator_55_eq, comparator_56_eq);
  Multiplexer #(.width(6), .enable("false")) multiplexer_22 (
    .in0({6{1'b0}}), .in1(6'b010110), .out(multiplexer_22_out), .sel(and_22_out));
  and and_22 (and_22_out, comparator_57_eq, comparator_58_eq);
  Multiplexer #(.width(6), .enable("false")) multiplexer_23 (
    .in0({6{1'b0}}), .in1(6'b010111), .out(multiplexer_23_out), .sel(and_23_out));
  and and_23 (and_23_out, comparator_59_eq, comparator_60_eq, comparator_61_eq);
  Multiplexer #(.width(6), .enable("false")) multiplexer_24 (
    .in0({6{1'b0}}), .in1(6'b011000), .out(multiplexer_24_out), .sel(and_24_out));
  and and_24 (and_24_out, comparator_62_eq, comparator_63_eq);
  Multiplexer #(.width(6), .enable("false")) multiplexer_25 (
    .in0({6{1'b0}}), .in1(6'b011001), .out(multiplexer_25_out), .sel(and_25_out));
  and and_25 (and_25_out, comparator_64_eq, comparator_65_eq);
  assign or_3_out = or_1_out | or_2_out;  // OR_Gate or_3, 6 bits wide
  not not_1 (not_1_out, BrEq);
  not not_2 (not_2_out, BrLT);
  not not_3 (not_3_out, BrLT);
  Comparator #(.width(7), .mode("unsigned")) comparator_66 (
    .a(Inst[6:0]), .b(7'b0100011), .eq(comparator_66_eq));  // open: gt, lt
  Comparator #(.width(3), .mode("unsigned")) comparator_67 (
    .a(Inst[14:12]), .b(3'b010), .eq(comparator_67_eq));  // open: gt, lt
  Comparator #(.width(7), .mode("unsigned")) comparator_68 (
    .a(Inst[6:0]), .b(7'b1100011), .eq(comparator_68_eq));  // open: gt, lt
  Comparator #(.width(3), .mode("unsigned")) comparator_69 (
    .a(Inst[14:12]), .b(3'b000), .eq(comparator_69_eq));  // open: gt, lt
  Comparator #(.width(7), .mode("unsigned")) comparator_70 (
    .a(Inst[6:0]), .b(7'b1100011), .eq(comparator_70_eq));  // open: gt, lt
  Comparator #(.width(3), .mode("unsigned")) comparator_71 (
    .a(Inst[14:12]), .b(3'b100), .eq(comparator_71_eq));  // open: gt, lt
  Comparator #(.width(7), .mode("unsigned")) comparator_72 (
    .a(Inst[6:0]), .b(7'b1100011), .eq(comparator_72_eq));  // open: gt, lt
  Comparator #(.width(3), .mode("unsigned")) comparator_73 (
    .a(Inst[14:12]), .b(3'b110), .eq(comparator_73_eq));  // open: gt, lt
  Comparator #(.width(7), .mode("unsigned")) comparator_74 (
    .a(Inst[6:0]), .b(7'b1100011), .eq(comparator_74_eq));  // open: gt, lt
  Comparator #(.width(3), .mode("unsigned")) comparator_75 (
    .a(Inst[14:12]), .b(3'b001), .eq(comparator_75_eq));  // open: gt, lt
  Comparator #(.width(7), .mode("unsigned")) comparator_76 (
    .a(Inst[6:0]), .b(7'b1100011), .eq(comparator_76_eq));  // open: gt, lt
  Comparator #(.width(3), .mode("unsigned")) comparator_77 (
    .a(Inst[14:12]), .b(3'b111), .eq(comparator_77_eq));  // open: gt, lt
  Comparator #(.width(7), .mode("unsigned")) comparator_78 (
    .a(Inst[6:0]), .b(7'b0010111), .eq(comparator_78_eq));  // open: gt, lt
  Comparator #(.width(7), .mode("unsigned")) comparator_79 (
    .a(Inst[6:0]), .b(7'b0110111), .eq(comparator_79_eq));  // open: gt, lt
  Comparator #(.width(7), .mode("unsigned")) comparator_80 (
    .a(Inst[6:0]), .b(7'b1101111), .eq(comparator_80_eq));  // open: gt, lt
  Comparator #(.width(7), .mode("unsigned")) comparator_81 (
    .a(Inst[6:0]), .b(7'b1100111), .eq(comparator_81_eq));  // open: gt, lt
  Comparator #(.width(3), .mode("unsigned")) comparator_82 (
    .a(Inst[14:12]), .b(3'b000), .eq(comparator_82_eq));  // open: gt, lt
  and and_26 (and_26_out, comparator_66_eq, comparator_67_eq);
  and and_27 (and_27_out, comparator_68_eq, not_1_out, comparator_69_eq);
  and and_28 (and_28_out, comparator_70_eq, not_2_out, comparator_71_eq);
  and and_29 (and_29_out, comparator_72_eq, not_3_out, comparator_73_eq);
  and and_30 (and_30_out, comparator_74_eq, BrEq, comparator_75_eq);
  and and_31 (and_31_out, comparator_76_eq, BrLT, comparator_77_eq);
  and and_32 (and_32_out, comparator_81_eq, comparator_82_eq);
  Multiplexer #(.width(6), .enable("false")) multiplexer_26 (
    .in0({6{1'b0}}), .in1(6'b011010), .out(multiplexer_26_out), .sel(and_26_out));
  Multiplexer #(.width(6), .enable("false")) multiplexer_27 (
    .in0({6{1'b0}}), .in1(6'b011011), .out(multiplexer_27_out), .sel(and_27_out));
  Multiplexer #(.width(6), .enable("false")) multiplexer_28 (
    .in0({6{1'b0}}), .in1(6'b011101), .out(multiplexer_28_out), .sel(and_28_out));
  Multiplexer #(.width(6), .enable("false")) multiplexer_29 (
    .in0({6{1'b0}}), .in1(6'b011111), .out(multiplexer_29_out), .sel(and_29_out));
  Multiplexer #(.width(6), .enable("false")) multiplexer_30 (
    .in0({6{1'b0}}), .in1(6'b100001), .out(multiplexer_30_out), .sel(and_30_out));
  Multiplexer #(.width(6), .enable("false")) multiplexer_31 (
    .in0({6{1'b0}}), .in1(6'b100011), .out(multiplexer_31_out), .sel(and_31_out));
  Multiplexer #(.width(6), .enable("false")) multiplexer_32 (
    .in0({6{1'b0}}), .in1(6'b100101), .out(multiplexer_32_out), .sel(comparator_78_eq));
  Multiplexer #(.width(6), .enable("false")) multiplexer_33 (
    .in0({6{1'b0}}), .in1(6'b100110), .out(multiplexer_33_out), .sel(comparator_79_eq));
  Multiplexer #(.width(6), .enable("false")) multiplexer_34 (
    .in0({6{1'b0}}), .in1(6'b100111), .out(multiplexer_34_out), .sel(comparator_80_eq));
  Multiplexer #(.width(6), .enable("false")) multiplexer_35 (
    .in0({6{1'b0}}), .in1(6'b101000), .out(multiplexer_35_out), .sel(and_32_out));
  not not_4 (not_4_out, BrEq);
  Comparator #(.width(7), .mode("unsigned")) comparator_83 (
    .a(Inst[6:0]), .b(7'b1100011), .eq(comparator_83_eq));  // open: gt, lt
  Comparator #(.width(3), .mode("unsigned")) comparator_84 (
    .a(Inst[14:12]), .b(3'b000), .eq(comparator_84_eq));  // open: gt, lt
  Comparator #(.width(7), .mode("unsigned")) comparator_85 (
    .a(Inst[6:0]), .b(7'b1100011), .eq(comparator_85_eq));  // open: gt, lt
  Comparator #(.width(3), .mode("unsigned")) comparator_86 (
    .a(Inst[14:12]), .b(3'b100), .eq(comparator_86_eq));  // open: gt, lt
  Comparator #(.width(7), .mode("unsigned")) comparator_87 (
    .a(Inst[6:0]), .b(7'b1100011), .eq(comparator_87_eq));  // open: gt, lt
  Comparator #(.width(3), .mode("unsigned")) comparator_88 (
    .a(Inst[14:12]), .b(3'b110), .eq(comparator_88_eq));  // open: gt, lt
  Comparator #(.width(7), .mode("unsigned")) comparator_89 (
    .a(Inst[6:0]), .b(7'b1100011), .eq(comparator_89_eq));  // open: gt, lt
  Comparator #(.width(3), .mode("unsigned")) comparator_90 (
    .a(Inst[14:12]), .b(3'b001), .eq(comparator_90_eq));  // open: gt, lt
  Comparator #(.width(7), .mode("unsigned")) comparator_91 (
    .a(Inst[6:0]), .b(7'b1100011), .eq(comparator_91_eq));  // open: gt, lt
  Comparator #(.width(3), .mode("unsigned")) comparator_92 (
    .a(Inst[14:12]), .b(3'b111), .eq(comparator_92_eq));  // open: gt, lt
  and and_33 (and_33_out, comparator_83_eq, BrEq, comparator_84_eq);
  and and_34 (and_34_out, comparator_85_eq, BrLT, comparator_86_eq);
  and and_35 (and_35_out, comparator_87_eq, BrLT, comparator_88_eq);
  and and_36 (and_36_out, comparator_89_eq, not_4_out, comparator_90_eq);
  and and_37 (and_37_out, comparator_91_eq, BrLT, comparator_92_eq);
  Multiplexer #(.width(6), .enable("false")) multiplexer_36 (
    .in0({6{1'b0}}), .in1(6'b011100), .out(multiplexer_36_out), .sel(and_33_out));
  Multiplexer #(.width(6), .enable("false")) multiplexer_37 (
    .in0({6{1'b0}}), .in1(6'b011110), .out(multiplexer_37_out), .sel(and_34_out));
  Multiplexer #(.width(6), .enable("false")) multiplexer_38 (
    .in0({6{1'b0}}), .in1(6'b100000), .out(multiplexer_38_out), .sel(and_35_out));
  Multiplexer #(.width(6), .enable("false")) multiplexer_39 (
    .in0({6{1'b0}}), .in1(6'b100010), .out(multiplexer_39_out), .sel(and_36_out));
  Multiplexer #(.width(6), .enable("false")) multiplexer_40 (
    .in0({6{1'b0}}), .in1(6'b100100), .out(multiplexer_40_out), .sel(and_37_out));
  ROM #(.addrWidth(6), .dataWidth(18)) rom_1 (
    .addr(or_3_out), .data({PCSel, ImmSel, rom_1_data[13], ASel, BSel, MemRW, RegWEn, WBSel, ALUSel}));
  Comparator #(.width(3), .mode("unsigned")) comparator_93 (
    .a(Inst[14:12]), .b(3'b110), .eq(comparator_93_eq));  // open: gt, lt
  Comparator #(.width(3), .mode("unsigned")) comparator_94 (
    .a(Inst[14:12]), .b(3'b111), .eq(comparator_94_eq));  // open: gt, lt
  or or_4 (BrUn, comparator_93_eq, comparator_94_eq);

  // Other names for the same wires on the sheet: opcode[6:0] = Inst[6:0]; funct3[2:0] = Inst[14:12];
  //   funct7[6:0] = Inst[31:25]

  // Notes on the sheet:
  //   add
  //   mul
  //   sub
  //   sll
  //   mulh
  //   mulhu
  //   xor
  //   div
  //   divu
  //   srl
  //   or
  //   remu
  //   and
  //   xori
  //   andi
  //   lb
  //   lh
  //   lw
  //   lbu
  //   lhu
  //   addi
  //   slli
  //   slti
  //   slli
  //   ori
  //   sw
  //   beq
  //   blt
  //   bltu
  //   bne
  //   bgeu
  //   auipc
  //   lui
  //   jal
  //   jalr
  //   beq
  //   blt
  //   bltu
  //   bne
  //   bgeu
  //   contents of rom_1 (hex, n*v repeats v):
  //   0 d3 d5 d4 df d7 d6 d2 d9 d8 db d1 da d0 543 5c3 4c3 643 6c3 4d3 4df 4dd 4d2 4db 4d1 4d0 4403 8c83
  //   28c83 8c83 28c83 ac83 2ac83 8c83 28c83 ac83 2ac83 ccd3 d4d3 30ce3 204e3
endmodule

module imm (
  input  [24:0] Inst31to7,
  input  [2:0] ImmSel,
  output [31:0] Imm
);

  wire [31:0] B_type, I_type, J_type, S_type, U_type;

  Multiplexer #(.select(3), .width(32), .enable("false")) multiplexer_1 (
    .in0(I_type), .in1(S_type), .in2(B_type), .in3(U_type), .in4(J_type), .out(Imm), .sel(ImmSel));  // open: in5, in6, in7
  assign I_type = {{21{Inst31to7[24]}}, Inst31to7[23:13]};  // Bit_Extender bit_extender_1
  assign S_type = {{21{Inst31to7[24]}}, {Inst31to7[23:18], Inst31to7[4:0]}};  // Bit_Extender bit_extender_2
  assign B_type = {{20{Inst31to7[24]}}, {Inst31to7[0], Inst31to7[23:18], Inst31to7[4:1], 1'b0}};  // Bit_Extender bit_extender_3
  assign U_type = {{1{Inst31to7[24]}}, {Inst31to7[23:5], {12{1'b0}}}};  // Bit_Extender bit_extender_4
  assign J_type = {{12{Inst31to7[24]}}, {Inst31to7[12:5], Inst31to7[13], Inst31to7[23:14], 1'b0}};  // Bit_Extender bit_extender_5
  // Probe on B_type

  // Other names for the same wires on the sheet: Inst_8_11[3:0] = Inst31to7[4:1]; Inst_7 = Inst31to7[0];
  //   Inst_21_24[3:0] = Inst31to7[17:14]; Inst_25_30[5:0] = Inst31to7[23:18]; Inst_20 = Inst31to7[13];
  //   Inst_12_19[7:0] = Inst31to7[12:5]; Inst_31 = Inst31to7[24]

  // Notes on the sheet:
  //   spliter
  //   use 0-4 to match ISBUJ
  //   INPUT
  //   OUTPUT
  //   000 = I
  //   001 = S
  //   010 = B
  //   011 = U
  //   100 = J
  //   I type
  //   S_type
  //   B_type
  //   U_type
  //   J_type
endmodule

module branch (
  input  [31:0] DataA,
  input  [31:0] DataB,
  input  BrUn,
  output BrEq,
  output BrLT
);

  wire comparator_1_lt, comparator_2_lt;

  Comparator #(.width(32)) comparator_1 (.a(DataA), .b(DataB), .eq(BrEq), .lt(comparator_1_lt));  // open: gt
  Comparator #(.width(32), .mode("unsigned")) comparator_2 (
    .a(DataA), .b(DataB), .lt(comparator_2_lt));  // open: gt, eq
  Multiplexer #(.enable("false")) multiplexer_1 (.in0(comparator_1_lt), .in1(comparator_2_lt), .out(BrLT), .sel(BrUn));
endmodule
