// Logisim project cpu_abandoned.circ as structural Verilog: 4 circuits, main circuit main
module main (
  input  [31:0] INSTRUCTION,
  input  CLOCK,
  output [31:0] FETCH_ADDRESS,
  output [31:0] ra,
  output [31:0] sp,
  output [31:0] t0,
  output [31:0] t1,
  output [31:0] t2,
  output [31:0] s0,
  output [31:0] s1,
  output [31:0] a0
);

  wire BrEq, BrLT, BrUn, BSel, PCSel, RegWEn;
  wire [1:0] ASel, WBSel;
  wire [2:0] ImmSel, MemRW;
  wire [3:0] ALUSel;
  wire [31:0] ALU_result, DataA, DataB, DMEM_result, imm31_0, multiplexer_1_out, multiplexer_2_out,
       multiplexer_3_out, PC_ADD_1, WB;

  Multiplexer #(.width(32), .enable("false")) multiplexer_1 (
    .in0(PC_ADD_1), .in1(ALU_result), .out(multiplexer_1_out), .sel(PCSel));
  Register #(.width(32)) PC (.D(multiplexer_1_out), .clk(CLOCK), .Q(FETCH_ADDRESS));  // open: en, clr
  Adder #(.width(32)) adder_1 (.a(32'h1), .b(FETCH_ADDRESS), .out(PC_ADD_1));  // open: cin, cout
  control Control_logic (
    .ALUSel(ALUSel), .BSel(BSel), .ASel(ASel), .BrUn(BrUn), .PCSel(PCSel), .ImmSel(ImmSel), .BrLT(BrLT),
    .BrEq(BrEq), .Inst(INSTRUCTION), .MemRW(MemRW), .RegWEn(RegWEn), .WBSel(WBSel));
  imm Imm_GEN (.Imm(imm31_0), .Inst31to7(INSTRUCTION[31:7]), .ImmSel(ImmSel));
  regfile_main RegFile (
    .rs2(INSTRUCTION[24:20]), .rd(INSTRUCTION[11:7]), .Read_Data_1(DataA), .Read_Data_2(DataB), .ra(ra),
    .sp(sp), .t0(t0), .t1(t1), .t2(t2), .s0(s0), .s1(s1), .a0(a0), .rs1(INSTRUCTION[19:15]), .Write_Data(WB),
    .RegWEn(RegWEn), .clk(CLOCK));
  Multiplexer #(.width(32), .enable("false")) multiplexer_2 (
    .in0(DataB), .in1(imm31_0), .out(multiplexer_2_out), .sel(BSel));
  branch Branch_Comp (.BrLT(BrLT), .BrEq(BrEq), .DataB(DataB), .DataA(DataA));
  Multiplexer #(.select(2), .width(32), .enable("false")) multiplexer_3 (
    .in0(DataA), .in1(FETCH_ADDRESS), .in2({32{1'b0}}), .out(multiplexer_3_out), .sel(ASel));  // open: in3
  alu Arithmetic_Logic_Unit (.A(multiplexer_3_out), .B(multiplexer_2_out), .ALUSel(ALUSel), .Result(ALU_result));
  mem_main DMEM (.WriteAddr(ALU_result), .WriteData(DataB), .MemRW(MemRW), .ReadData(DMEM_result), .clk(CLOCK));
  Multiplexer #(.select(2), .width(32), .enable("false")) multiplexer_4 (
    .in0(DMEM_result), .in1(ALU_result), .in2(PC_ADD_1), .out(WB), .sel(WBSel));  // open: in3

  // Other names for the same wires on the sheet: clk = CLOCK; fetch_addr[31:0] = FETCH_ADDRESS

  // Notes on the sheet:
  //   Output
  //   Inputs/Outputs from run.circ. DO NOT MOVE THESE.
  //   Inputs
  //   Inputs/Outputs from run.circ. DO NOT MOVE THESE.
endmodule

module control (
  input  [31:0] Inst,
  input  BrEq,
  input  BrLT,
  output [2:0] ImmSel,
  output PCSel,
  output BrUn,
  output [1:0] ASel,
  output BSel,
  output [3:0] ALUSel,
  output [2:0] MemRW,
  output RegWEn,
  output [1:0] WBSel
);

  wire and_1_out, and_2_out, and_3_out, and_4_out, and_5_out, and_6_out, and_7_out, and_8_out, and_9_out,
       and_10_out, and_11_out, and_12_out, and_13_out, and_14_out, and_15_out, and_16_out, and_17_out,
       and_18_out, and_19_out, and_20_out, and_21_out, and_22_out, and_23_out, and_24_out, and_25_out,
       and_26_out, and_27_out, and_28_out, and_29_out, and_30_out, and_31_out, and_32_out, and_33_out,
       and_34_out, and_35_out, comparator_1_eq, comparator_2_eq, comparator_3_eq, comparator_4_eq,
       comparator_5_eq, comparator_6_eq, comparator_7_eq, comparator_8_eq, comparator_9_eq, comparator_10_eq,
       comparator_11_eq, comparator_12_eq, comparator_13_eq, comparator_14_eq, comparator_15_eq,
       comparator_16_eq, comparator_17_eq, comparator_18_eq, comparator_19_eq, comparator_20_eq,
       comparator_21_eq, comparator_22_eq, comparator_23_eq, comparator_24_eq, comparator_25_eq,
       comparator_26_eq, comparator_27_eq, comparator_28_eq, comparator_29_eq, comparator_30_eq,
       comparator_31_eq, comparator_32_eq, comparator_33_eq, comparator_34_eq, comparator_35_eq,
       comparator_36_eq, comparator_37_eq, comparator_38_eq, comparator_39_eq, comparator_40_eq,
       comparator_41_eq, comparator_42_eq, comparator_43_eq, comparator_44_eq, comparator_45_eq,
       comparator_46_eq, comparator_47_eq, comparator_48_eq, comparator_49_eq, comparator_50_eq,
       comparator_51_eq, comparator_52_eq, comparator_53_eq, comparator_54_eq, comparator_55_eq,
       comparator_56_eq, comparator_57_eq, comparator_58_eq, comparator_59_eq, comparator_60_eq,
       comparator_61_eq, comparator_62_eq, comparator_63_eq, comparator_64_eq, comparator_65_eq,
       comparator_66_eq, comparator_67_eq, comparator_68_eq, comparator_69_eq, comparator_70_eq,
       comparator_71_eq, comparator_72_eq, comparator_73_eq, comparator_74_eq, comparator_75_eq,
       comparator_76_eq, comparator_77_eq, comparator_78_eq, comparator_79_eq, comparator_80_eq,
       comparator_81_eq, comparator_82_eq, comparator_84_gt, comparator_85_lt, comparator_86_eq,
       comparator_87_gt, comparator_88_lt, comparator_89_gt, comparator_90_gt, comparator_91_lt,
       comparator_92_eq, comparator_93_eq, comparator_94_eq, comparator_95_eq, comparator_96_eq,
       comparator_97_gt, comparator_97_lt, multiplexer_44_out, undriven, undriven_2;
  wire [1:0] multiplexer_38_out, multiplexer_40_out;
  wire [2:0] multiplexer_36_out, multiplexer_37_out, multiplexer_43_out;
  wire [5:0] demultiplexer_1_out0, demultiplexer_1_out1, Inst_ID, multiplexer_1_out, multiplexer_2_out,
       multiplexer_3_out, multiplexer_4_out, multiplexer_5_out, multiplexer_6_out, multiplexer_7_out,
       multiplexer_8_out, multiplexer_9_out, multiplexer_10_out, multiplexer_11_out, multiplexer_12_out,
       multiplexer_13_out, multiplexer_14_out, multiplexer_15_out, multiplexer_16_out, multiplexer_17_out,
       multiplexer_18_out, multiplexer_19_out, multiplexer_20_out, multiplexer_21_out, multiplexer_22_out,
       multiplexer_23_out, multiplexer_24_out, multiplexer_25_out, multiplexer_26_out, multiplexer_27_out,
       multiplexer_28_out, multiplexer_29_out, multiplexer_30_out, multiplexer_31_out, multiplexer_32_out,
       multiplexer_33_out, multiplexer_34_out, multiplexer_35_out, or_1_out, or_2_out;

  Comparator #(.width(7)) comparator_1 (.a(Inst[6:0]), .b(7'b0110011), .eq(comparator_1_eq));  // open: gt, lt
  Comparator #(.width(3)) comparator_2 (.a(Inst[14:12]), .b(3'b000), .eq(comparator_2_eq));  // open: gt, lt
  Comparator #(.width(7)) comparator_3 (.a(Inst[31:25]), .b({7{1'b0}}), .eq(comparator_3_eq));  // open: gt, lt
  Comparator #(.width(7)) comparator_4 (.a(Inst[6:0]), .b(7'b0110011), .eq(comparator_4_eq));  // open: gt, lt
  Comparator #(.width(3)) comparator_5 (.a(Inst[14:12]), .b(3'b000), .eq(comparator_5_eq));  // open: gt, lt
  Comparator #(.width(7)) comparator_6 (.a(Inst[31:25]), .b(7'b0000001), .eq(comparator_6_eq));  // open: gt, lt
  Comparator #(.width(7)) comparator_7 (.a(Inst[6:0]), .b(7'b0110011), .eq(comparator_7_eq));  // open: gt, lt
  Comparator #(.width(3)) comparator_8 (.a(Inst[14:12]), .b(3'b000), .eq(comparator_8_eq));  // open: gt, lt
  Comparator #(.width(7)) comparator_9 (.a(Inst[31:25]), .b(7'b0100000), .eq(comparator_9_eq));  // open: gt, lt
  Comparator #(.width(7)) comparator_10 (.a(Inst[6:0]), .b(7'b0110011), .eq(comparator_10_eq));  // open: gt, lt
  Comparator #(.width(3)) comparator_11 (.a(Inst[14:12]), .b(3'b001), .eq(comparator_11_eq));  // open: gt, lt
  Comparator #(.width(7)) comparator_12 (.a(Inst[31:25]), .b({7{1'b0}}), .eq(comparator_12_eq));  // open: gt, lt
  Comparator #(.width(7)) comparator_13 (.a(Inst[6:0]), .b(7'b0110011), .eq(comparator_13_eq));  // open: gt, lt
  Comparator #(.width(3)) comparator_14 (.a(Inst[14:12]), .b(3'b001), .eq(comparator_14_eq));  // open: gt, lt
  Comparator #(.width(7)) comparator_15 (.a(Inst[31:25]), .b(7'b0000001), .eq(comparator_15_eq));  // open: gt, lt
  Comparator #(.width(7)) comparator_16 (.a(Inst[6:0]), .b(7'b0110011), .eq(comparator_16_eq));  // open: gt, lt
  Comparator #(.width(3)) comparator_17 (.a(Inst[14:12]), .b(3'b011), .eq(comparator_17_eq));  // open: gt, lt
  Comparator #(.width(7)) comparator_18 (.a(Inst[31:25]), .b(7'b0000001), .eq(comparator_18_eq));  // open: gt, lt
  Comparator #(.width(7)) comparator_19 (.a(Inst[6:0]), .b(7'b0110011), .eq(comparator_19_eq));  // open: gt, lt
  Comparator #(.width(3)) comparator_20 (.a(Inst[14:12]), .b(3'b100), .eq(comparator_20_eq));  // open: gt, lt
  Comparator #(.width(7)) comparator_21 (.a(Inst[31:25]), .b({7{1'b0}}), .eq(comparator_21_eq));  // open: gt, lt
  Comparator #(.width(7)) comparator_22 (.a(Inst[6:0]), .b(7'b0110011), .eq(comparator_22_eq));  // open: gt, lt
  Comparator #(.width(3)) comparator_23 (.a(Inst[14:12]), .b(3'b100), .eq(comparator_23_eq));  // open: gt, lt
  Comparator #(.width(7)) comparator_24 (.a(Inst[31:25]), .b(7'b0000001), .eq(comparator_24_eq));  // open: gt, lt
  Comparator #(.width(7)) comparator_25 (.a(Inst[6:0]), .b(7'b0110011), .eq(comparator_25_eq));  // open: gt, lt
  Comparator #(.width(3)) comparator_26 (.a(Inst[14:12]), .b(3'b101), .eq(comparator_26_eq));  // open: gt, lt
  Comparator #(.width(7)) comparator_27 (.a(Inst[31:25]), .b(7'b0000001), .eq(comparator_27_eq));  // open: gt, lt
  Comparator #(.width(7)) comparator_28 (.a(Inst[6:0]), .b(7'b0110011), .eq(comparator_28_eq));  // open: gt, lt
  Comparator #(.width(3)) comparator_29 (.a(Inst[14:12]), .b(3'b101), .eq(comparator_29_eq));  // open: gt, lt
  Comparator #(.width(7)) comparator_30 (.a(Inst[31:25]), .b({7{1'b0}}), .eq(comparator_30_eq));  // open: gt, lt
  Comparator #(.width(7)) comparator_31 (.a(Inst[6:0]), .b(7'b0110011), .eq(comparator_31_eq));  // open: gt, lt
  Comparator #(.width(3)) comparator_32 (.a(Inst[14:12]), .b(3'b110), .eq(comparator_32_eq));  // open: gt, lt
  Comparator #(.width(7)) comparator_33 (.a(Inst[31:25]), .b({7{1'b0}}), .eq(comparator_33_eq));  // open: gt, lt
  Comparator #(.width(7)) comparator_34 (.a(Inst[6:0]), .b(7'b0110011), .eq(comparator_34_eq));  // open: gt, lt
  Comparator #(.width(3)) comparator_35 (.a(Inst[14:12]), .b(3'b111), .eq(comparator_35_eq));  // open: gt, lt
  Comparator #(.width(7)) comparator_36 (.a(Inst[31:25]), .b(7'b0000001), .eq(comparator_36_eq));  // open: gt, lt
  Comparator #(.width(7)) comparator_37 (.a(Inst[6:0]), .b(7'b0110011), .eq(comparator_37_eq));  // open: gt, lt
  Comparator #(.width(3)) comparator_38 (.a(Inst[14:12]), .b(3'b111), .eq(comparator_38_eq));  // open: gt, lt
  Comparator #(.width(7)) comparator_39 (.a(Inst[31:25]), .b({7{1'b0}}), .eq(comparator_39_eq));  // open: gt, lt
  // Probe on Inst[6:0]
  and and_1 (and_1_out, comparator_1_eq, comparator_2_eq, comparator_3_eq);
  and and_2 (and_2_out, comparator_4_eq, comparator_5_eq, comparator_6_eq);
  and and_3 (and_3_out, comparator_7_eq, comparator_8_eq, comparator_9_eq);
  and and_4 (and_4_out, comparator_10_eq, comparator_11_eq, comparator_12_eq);
  and and_5 (and_5_out, comparator_13_eq, comparator_14_eq, comparator_15_eq);
  and and_6 (and_6_out, comparator_16_eq, comparator_17_eq, comparator_18_eq);
  and and_7 (and_7_out, comparator_19_eq, comparator_20_eq, comparator_21_eq);
  and and_8 (and_8_out, comparator_22_eq, comparator_23_eq, comparator_24_eq);
  and and_9 (and_9_out, comparator_25_eq, comparator_26_eq, comparator_27_eq);
  and and_10 (and_10_out, comparator_28_eq, comparator_29_eq, comparator_30_eq);
  and and_11 (and_11_out, comparator_31_eq, comparator_32_eq, comparator_33_eq);
  and and_12 (and_12_out, comparator_34_eq, comparator_35_eq, comparator_36_eq);
  and and_13 (and_13_out, comparator_37_eq, comparator_38_eq, comparator_39_eq);
  Multiplexer #(.width(6), .enable("false")) multiplexer_1 (
    .in0({6{1'b0}}), .in1(6'b000001), .out(multiplexer_1_out), .sel(and_1_out));
  Multiplexer #(.width(6), .enable("false")) multiplexer_2 (
    .in0({6{1'b0}}), .in1(6'b000010), .out(multiplexer_2_out), .sel(and_2_out));
  Multiplexer #(.width(6), .enable("false")) multiplexer_3 (
    .in0({6{1'b0}}), .in1(6'b000011), .out(multiplexer_3_out), .sel(and_3_out));
  Multiplexer #(.width(6), .enable("false")) multiplexer_4 (
    .in0({6{1'b0}}), .in1(6'b000100), .out(multiplexer_4_out), .sel(and_4_out));
  Multiplexer #(.width(6), .enable("false")) multiplexer_5 (
    .in0({6{1'b0}}), .in1(6'b000101), .out(multiplexer_5_out), .sel(and_5_out));
  Multiplexer #(.width(6), .enable("false")) multiplexer_6 (
    .in0({6{1'b0}}), .in1(6'b000110), .out(multiplexer_6_out), .sel(and_6_out));
  Multiplexer #(.width(6), .enable("false")) multiplexer_7 (
    .in0({6{1'b0}}), .in1(6'b000111), .out(multiplexer_7_out), .sel(and_7_out));
  Multiplexer #(.width(6), .enable("false")) multiplexer_8 (
    .in0({6{1'b0}}), .in1(6'b001000), .out(multiplexer_8_out), .sel(and_8_out));
  Multiplexer #(.width(6), .enable("false")) multiplexer_9 (
    .in0({6{1'b0}}), .in1(6'b001001), .out(multiplexer_9_out), .sel(and_9_out));
  Multiplexer #(.width(6), .enable("false")) multiplexer_10 (
    .in0({6{1'b0}}), .in1(6'b001010), .out(multiplexer_10_out), .sel(and_10_out));
  Multiplexer #(.width(6), .enable("false")) multiplexer_11 (
    .in0({6{1'b0}}), .in1(6'b001011), .out(multiplexer_11_out), .sel(and_11_out));
  Multiplexer #(.width(6), .enable("false")) multiplexer_12 (
    .in0({6{1'b0}}), .in1(6'b001100), .out(multiplexer_12_out), .sel(and_12_out));
  Multiplexer #(.width(6), .enable("false")) multiplexer_13 (
    .in0({6{1'b0}}), .in1(6'b001101), .out(multiplexer_13_out), .sel(and_13_out));
  assign or_1_out = multiplexer_1_out | multiplexer_2_out | multiplexer_3_out | multiplexer_4_out | multiplexer_5_out | multiplexer_6_out | multiplexer_7_out | multiplexer_8_out | multiplexer_9_out | multiplexer_10_out | multiplexer_11_out | multiplexer_12_out | multiplexer_13_out | multiplexer_14_out | multiplexer_15_out | multiplexer_16_out | multiplexer_17_out | multiplexer_18_out | multiplexer_19_out | multiplexer_20_out | multiplexer_21_out | multiplexer_22_out | multiplexer_23_out | multiplexer_24_out | multiplexer_25_out | multiplexer_26_out | multiplexer_27_out | multiplexer_28_out | multiplexer_29_out | multiplexer_30_out | multiplexer_31_out | multiplexer_32_out;  // OR_Gate or_1, 6 bits wide
  assign or_2_out = multiplexer_33_out | multiplexer_34_out | multiplexer_35_out;  // OR_Gate or_2, 6 bits wide
  Comparator #(.width(7)) comparator_40 (.a(Inst[6:0]), .b(7'b0000011), .eq(comparator_40_eq));  // open: gt, lt
  Comparator #(.width(3)) comparator_41 (.a(Inst[14:12]), .b(3'b000), .eq(comparator_41_eq));  // open: gt, lt
  Comparator #(.width(7)) comparator_42 (.a(Inst[6:0]), .b(7'b0000011), .eq(comparator_42_eq));  // open: gt, lt
  Comparator #(.width(3)) comparator_43 (.a(Inst[14:12]), .b(3'b001), .eq(comparator_43_eq));  // open: gt, lt
  Comparator #(.width(7)) comparator_44 (.a(Inst[6:0]), .b(7'b0000011), .eq(comparator_44_eq));  // open: gt, lt
  Comparator #(.width(3)) comparator_45 (.a(Inst[14:12]), .b(3'b010), .eq(comparator_45_eq));  // open: gt, lt
  Comparator #(.width(7)) comparator_46 (.a(Inst[6:0]), .b(7'b0000011), .eq(comparator_46_eq));  // open: gt, lt
  Comparator #(.width(3)) comparator_47 (.a(Inst[14:12]), .b(3'b100), .eq(comparator_47_eq));  // open: gt, lt
  Comparator #(.width(7)) comparator_48 (.a(Inst[6:0]), .b(7'b0000011), .eq(comparator_48_eq));  // open: gt, lt
  Comparator #(.width(3)) comparator_49 (.a(Inst[14:12]), .b(3'b101), .eq(comparator_49_eq));  // open: gt, lt
  Comparator #(.width(7)) comparator_50 (.a(Inst[6:0]), .b(7'b0010011), .eq(comparator_50_eq));  // open: gt, lt
  Comparator #(.width(3)) comparator_51 (.a(Inst[14:12]), .b(3'b000), .eq(comparator_51_eq));  // open: gt, lt
  Comparator #(.width(7)) comparator_52 (.a(Inst[6:0]), .b(7'b0010011), .eq(comparator_52_eq));  // open: gt, lt
  Comparator #(.width(3)) comparator_53 (.a(Inst[14:12]), .b(3'b001), .eq(comparator_53_eq));  // open: gt, lt
  Comparator #(.width(7)) comparator_54 (.a(Inst[31:25]), .b({7{1'b0}}), .eq(comparator_54_eq));  // open: gt, lt
  Comparator #(.width(7)) comparator_55 (.a(Inst[6:0]), .b(7'b0010011), .eq(comparator_55_eq));  // open: gt, lt
  Comparator #(.width(3)) comparator_56 (.a(Inst[14:12]), .b(3'b010), .eq(comparator_56_eq));  // open: gt, lt
  Comparator #(.width(7)) comparator_57 (.a(Inst[6:0]), .b(7'b0010011), .eq(comparator_57_eq));  // open: gt, lt
  Comparator #(.width(3)) comparator_58 (.a(Inst[14:12]), .b(3'b100), .eq(comparator_58_eq));  // open: gt, lt
  Comparator #(.width(7)) comparator_59 (.a(Inst[6:0]), .b(7'b0010011), .eq(comparator_59_eq));  // open: gt, lt
  Comparator #(.width(3)) comparator_60 (.a(Inst[14:12]), .b(3'b101), .eq(comparator_60_eq));  // open: gt, lt
  Comparator #(.width(7)) comparator_61 (.a(Inst[31:25]), .b({7{1'b0}}), .eq(comparator_61_eq));  // open: gt, lt
  Comparator #(.width(7)) comparator_62 (.a(Inst[6:0]), .b(7'b0010011), .eq(comparator_62_eq));  // open: gt, lt
  Comparator #(.width(3)) comparator_63 (.a(Inst[14:12]), .b(3'b110), .eq(comparator_63_eq));  // open: gt, lt
  Comparator #(.width(7)) comparator_64 (.a(Inst[6:0]), .b(7'b0010011), .eq(comparator_64_eq));  // open: gt, lt
  Comparator #(.width(3)) comparator_65 (.a(Inst[14:12]), .b(3'b111), .eq(comparator_65_eq));  // open: gt, lt
  Multiplexer #(.width(6), .enable("false")) multiplexer_14 (
    .in0({6{1'b0}}), .in1(6'b001110), .out(multiplexer_14_out), .sel(and_14_out));
  and and_14 (and_14_out, comparator_40_eq, comparator_41_eq);
  Multiplexer #(.width(6), .enable("false")) multiplexer_15 (
    .in0({6{1'b0}}), .in1(6'b001111), .out(multiplexer_15_out), .sel(and_15_out));
  and and_15 (and_15_out, comparator_42_eq, comparator_43_eq);
  Multiplexer #(.width(6), .enable("false")) multiplexer_16 (
    .in0({6{1'b0}}), .in1(6'b010000), .out(multiplexer_16_out), .sel(and_16_out));
  and and_16 (and_16_out, comparator_44_eq, comparator_45_eq);
  Multiplexer #(.width(6), .enable("false")) multiplexer_17 (
    .in0({6{1'b0}}), .in1(6'b010001), .out(multiplexer_17_out), .sel(and_17_out));
  and and_17 (and_17_out, comparator_46_eq, comparator_47_eq);
  Multiplexer #(.width(6), .enable("false")) multiplexer_18 (
    .in0({6{1'b0}}), .in1(6'b010010), .out(multiplexer_18_out), .sel(and_18_out));
  and and_18 (and_18_out, comparator_48_eq, comparator_49_eq);
  Multiplexer #(.width(6), .enable("false")) multiplexer_19 (
    .in0({6{1'b0}}), .in1(6'b010011), .out(multiplexer_19_out), .sel(and_19_out));
  and and_19 (and_19_out, comparator_50_eq, comparator_51_eq);
  Multiplexer #(.width(6), .enable("false")) multiplexer_20 (
    .in0({6{1'b0}}), .in1(6'b010100), .out(multiplexer_20_out), .sel(and_20_out));
  and and_20 (and_20_out, comparator_52_eq, comparator_53_eq, comparator_54_eq);
  Multiplexer #(.width(6), .enable("false")) multiplexer_21 (
    .in0({6{1'b0}}), .in1(6'b010101), .out(multiplexer_21_out), .sel(and_21_out));
  and and_21 (and_21_out, comparator_55_eq, comparator_56_eq);
  Multiplexer #(.width(6), .enable("false")) multiplexer_22 (
    .in0({6{1'b0}}), .in1(6'b010110), .out(multiplexer_22_out), .sel(and_22_out));
  and and_22 (and_22_out, comparator_57_eq, comparator_58_eq);
  Multiplexer #(.width(6), .enable("false")) multiplexer_23 (
    .in0({6{1'b0}}), .in1(6'b010111), .out(multiplexer_23_out), .sel(and_23_out));
  and and_23 (and_23_out, comparator_59_eq, comparator_60_eq, comparator_61_eq);
  Multiplexer #(.width(6), .enable("false")) multiplexer_24 (
    .in0({6{1'b0}}), .in1(6'b011000), .out(multiplexer_24_out), .sel(and_24_out));
  and and_24 (and_24_out, comparator_62_eq, comparator_63_eq);
  Multiplexer #(.width(6), .enable("false")) multiplexer_25 (
    .in0({6{1'b0}}), .in1(6'b011001), .out(multiplexer_25_out), .sel(and_25_out));
  and and_25 (and_25_out, comparator_64_eq, comparator_65_eq);
  assign Inst_ID = or_1_out | or_2_out;  // OR_Gate or_3, 6 bits wide
  Comparator #(.width(7)) comparator_66 (.a(Inst[6:0]), .b(7'b0100011), .eq(comparator_66_eq));  // open: gt, lt
  Comparator #(.width(3)) comparator_67 (.a(Inst[14:12]), .b(3'b010), .eq(comparator_67_eq));  // open: gt, lt
  Comparator #(.width(7)) comparator_68 (.a(Inst[6:0]), .b(7'b1100011), .eq(comparator_68_eq));  // open: gt, lt
  Comparator #(.width(3)) comparator_69 (.a(Inst[14:12]), .b(3'b000), .eq(comparator_69_eq));  // open: gt, lt
  Comparator #(.width(7)) comparator_70 (.a(Inst[6:0]), .b(7'b1100011), .eq(comparator_70_eq));  // open: gt, lt
  Comparator #(.width(3)) comparator_71 (.a(Inst[14:12]), .b(3'b100), .eq(comparator_71_eq));  // open: gt, lt
  Comparator #(.width(7)) comparator_72 (.a(Inst[6:0]), .b(7'b1100011), .eq(comparator_72_eq));  // open: gt, lt
  Comparator #(.width(3)) comparator_73 (.a(Inst[14:12]), .b(3'b110), .eq(comparator_73_eq));  // open: gt, lt
  Comparator #(.width(7)) comparator_74 (.a(Inst[6:0]), .b(7'b1100011), .eq(comparator_74_eq));  // open: gt, lt
  Comparator #(.width(3)) comparator_75 (.a(Inst[14:12]), .b(3'b001), .eq(comparator_75_eq));  // open: gt, lt
  Comparator #(.width(7)) comparator_76 (.a(Inst[6:0]), .b(7'b1100011), .eq(comparator_76_eq));  // open: gt, lt
  Comparator #(.width(3)) comparator_77 (.a(Inst[14:12]), .b(3'b111), .eq(comparator_77_eq));  // open: gt, lt
  Comparator #(.width(7)) comparator_78 (.a(Inst[6:0]), .b(7'b0010111), .eq(comparator_78_eq));  // open: gt, lt
  Comparator #(.width(7)) comparator_79 (.a(Inst[6:0]), .b(7'b0110111), .eq(comparator_79_eq));  // open: gt, lt
  Comparator #(.width(7)) comparator_80 (.a(Inst[6:0]), .b(7'b1101111), .eq(comparator_80_eq));  // open: gt, lt
  Comparator #(.width(7)) comparator_81 (.a(Inst[6:0]), .b(7'b1100111), .eq(comparator_81_eq));  // open: gt, lt
  Comparator #(.width(3)) comparator_82 (.a(Inst[14:12]), .b(3'b000), .eq(comparator_82_eq));  // open: gt, lt
  and and_26 (and_26_out, comparator_66_eq, comparator_67_eq);
  and and_27 (and_27_out, comparator_68_eq, comparator_69_eq);
  and and_28 (and_28_out, comparator_70_eq, comparator_71_eq);
  and and_29 (and_29_out, comparator_72_eq, comparator_73_eq);
  and and_30 (and_30_out, comparator_74_eq, comparator_75_eq);
  and and_31 (and_31_out, comparator_76_eq, comparator_77_eq);
  and and_32 (and_32_out, comparator_81_eq, comparator_82_eq);
  Multiplexer #(.width(6), .enable("false")) multiplexer_26 (
    .in0({6{1'b0}}), .in1(6'b011010), .out(multiplexer_26_out), .sel(and_26_out));
  Multiplexer #(.width(6), .enable("false")) multiplexer_27 (
    .in0({6{1'b0}}), .in1(6'b011011), .out(multiplexer_27_out), .sel(and_27_out));
  Multiplexer #(.width(6), .enable("false")) multiplexer_28 (
    .in0({6{1'b0}}), .in1(6'b011100), .out(multiplexer_28_out), .sel(and_28_out));
  Multiplexer #(.width(6), .enable("false")) multiplexer_29 (
    .in0({6{1'b0}}), .in1(6'b011101), .out(multiplexer_29_out), .sel(and_29_out));
  Multiplexer #(.width(6), .enable("false")) multiplexer_30 (
    .in0({6{1'b0}}), .in1(6'b011110), .out(multiplexer_30_out), .sel(and_30_out));
  Multiplexer #(.width(6), .enable("false")) multiplexer_31 (
    .in0({6{1'b0}}), .in1(6'b011111), .out(multiplexer_31_out), .sel(and_31_out));
  Multiplexer #(.width(6), .enable("false")) multiplexer_32 (
    .in0({6{1'b0}}), .in1(6'b100000), .out(multiplexer_32_out), .sel(comparator_78_eq));
  Multiplexer #(.width(6), .enable("false")) multiplexer_33 (
    .in0({6{1'b0}}), .in1(6'b100001), .out(multiplexer_33_out), .sel(comparator_79_eq));
  Multiplexer #(.width(6), .enable("false")) multiplexer_34 (
    .in0({6{1'b0}}), .in1(6'b100010), .out(multiplexer_34_out), .sel(comparator_80_eq));
  Multiplexer #(.width(6), .enable("false")) multiplexer_35 (
    .in0({6{1'b0}}), .in1(6'b100011), .out(multiplexer_35_out), .sel(and_32_out));
  Demultiplexer #(.width(6), .enable("false")) demultiplexer_1 (
    .out0(demultiplexer_1_out0), .out1(demultiplexer_1_out1), .in(Inst_ID), .sel(Inst_ID[5]));
  Multiplexer #(.select(5), .width(3), .enable("false")) multiplexer_36 (
    .in0(3'b000), .in1(3'b000), .in2(3'b000), .in3(3'b000), .in4(3'b000), .in5(3'b000), .in6(3'b000),
    .in7(3'b000), .in8(3'b000), .in9(3'b000), .in10(3'b000), .in11(3'b000), .in12(3'b000), .in13(3'b000),
    .in14(3'b000), .in15(3'b000), .in16(3'b000), .in17(3'b000), .in18(3'b000), .in19(3'b000), .in20(3'b000),
    .in21(3'b000), .in22(3'b000), .in23(3'b000), .in24(3'b000), .in25(3'b000), .in26(3'b001), .in27(3'b010),
    .in28(3'b010), .in29(3'b010), .in30(3'b010), .in31(3'b010), .out(multiplexer_36_out),
    .sel(demultiplexer_1_out0[4:0]));
  Multiplexer #(.select(5), .width(3), .enable("false")) multiplexer_37 (
    .in0(3'b011), .in1(3'b011), .in2(3'b100), .in3(3'b000), .in4(3'b000), .in5(3'b000), .in6(3'b000),
    .in7(3'b000), .in8(3'b000), .in9(3'b000), .in10(3'b000), .in11(3'b000), .in12(3'b000), .in13(3'b000),
    .in14(3'b000), .in15(3'b000), .in16(3'b000), .in17(3'b000), .in18(3'b000), .in19(3'b000), .in20(3'b000),
    .in21(3'b000), .in22(3'b000), .in23(3'b000), .in24(3'b000), .in25(3'b000), .in26(3'b000), .in27(3'b000),
    .in28(3'b000), .in29(3'b000), .in30(3'b000), .in31(3'b000), .out(multiplexer_37_out),
    .sel(demultiplexer_1_out1[4:0]));
  assign ImmSel = multiplexer_36_out | multiplexer_37_out;  // OR_Gate or_4, 3 bits wide
  ROM rom_1 ();  // open: addr, data
  Comparator #(.width(6), .mode("unsigned")) comparator_83 (.a(Inst_ID), .b(6'b010100), .lt(BSel));  // open: gt, eq
  Comparator #(.width(6), .mode("unsigned")) comparator_84 (
    .a(Inst_ID), .b(6'b011010), .gt(comparator_84_gt));  // open: eq, lt
  Comparator #(.width(6), .mode("unsigned")) comparator_85 (
    .a(Inst_ID), .b(6'b100011), .lt(comparator_85_lt));  // open: gt, eq
  Comparator #(.width(6), .mode("unsigned")) comparator_86 (
    .a(Inst_ID), .b(6'b100001), .eq(comparator_86_eq));  // open: gt, lt
  Multiplexer #(.width(2), .enable("false")) multiplexer_38 (
    .in0(2'b00), .in1(2'b01), .out(multiplexer_38_out), .sel(and_33_out));
  and and_33 (and_33_out, comparator_84_gt, comparator_85_lt);
  Comparator #(.width(6), .mode("unsigned")) comparator_87 (
    .a(Inst_ID), .b(6'b001101), .gt(comparator_87_gt));  // open: eq, lt
  Comparator #(.width(6), .mode("unsigned")) comparator_88 (
    .a(Inst_ID), .b(6'b010011), .lt(comparator_88_lt));  // open: gt, eq
  Multiplexer #(.width(2), .enable("false")) multiplexer_39 (
    .in0(multiplexer_38_out), .in1(2'b10), .out(ASel), .sel(comparator_86_eq));
  and and_34 (and_34_out, comparator_87_gt, comparator_88_lt);
  Comparator #(.width(6), .mode("unsigned")) comparator_89 (
    .a(Inst_ID), .b(6'b100010), .gt(comparator_89_gt));  // open: eq, lt
  Multiplexer #(.width(2), .enable("false")) multiplexer_40 (
    .in0(2'b01), .in1(2'b00), .out(multiplexer_40_out), .sel(and_34_out));
  Comparator #(.width(6), .mode("unsigned")) comparator_90 (
    .a(Inst_ID), .b(6'b011001), .gt(comparator_90_gt));  // open: eq, lt
  and and_35 (and_35_out, comparator_90_gt, comparator_91_lt);
  Comparator #(.width(6), .mode("unsigned")) comparator_91 (
    .a(Inst_ID), .b(6'b100000), .lt(comparator_91_lt));  // open: gt, eq
  Multiplexer #(.width(2), .enable("false")) multiplexer_41 (
    .in0(multiplexer_40_out), .in1(2'b10), .out(WBSel), .sel(comparator_89_gt));
  Multiplexer #(.enable("false")) multiplexer_42 (.in0(1'b1), .in1(1'b0), .out(RegWEn), .sel(and_35_out));
  Multiplexer #(.select(5), .width(3), .enable("false")) multiplexer_43 (
    .in0(3'b001), .in1(3'b001), .in2(3'b001), .in3(3'b001), .in4(3'b001), .in5(3'b001), .in6(3'b001),
    .in7(3'b001), .in8(3'b001), .in9(3'b001), .in10(3'b001), .in11(3'b001), .in12(3'b001), .in13(3'b001),
    .in14(3'b010), .in15(3'b011), .in16(3'b000), .in17(3'b100), .in18(3'b101), .in19(3'b001), .in20(3'b001),
    .in21(3'b001), .in22(3'b001), .in23(3'b001), .in24(3'b001), .in25(3'b001), .in26(3'b000), .in27(3'b001),
    .in28(3'b001), .in29(3'b001), .in30(3'b001), .in31(3'b001), .out(multiplexer_43_out), .sel(Inst_ID[4:0]));
  Comparator #(.width(6), .mode("unsigned")) comparator_92 (
    .a(Inst_ID), .b(6'b011011), .eq(comparator_92_eq));  // open: gt, lt
  Comparator #(.width(6), .mode("unsigned")) comparator_93 (
    .a(Inst_ID), .b(6'b011100), .eq(comparator_93_eq));  // open: gt, lt
  Comparator #(.width(6), .mode("unsigned")) comparator_94 (
    .a(Inst_ID), .b(6'b011101), .eq(comparator_94_eq));  // open: gt, lt
  Comparator #(.width(6), .mode("unsigned")) comparator_95 (
    .a(Inst_ID), .b(6'b011110), .eq(comparator_95_eq));  // open: gt, lt
  Comparator #(.width(6), .mode("unsigned")) comparator_96 (
    .a(Inst_ID), .b(6'b011111), .eq(comparator_96_eq));  // open: gt, lt
  Comparator #(.width(6), .mode("unsigned")) comparator_97 (
    .a(Inst_ID), .b(6'b011011), .gt(comparator_97_gt), .lt(comparator_97_lt));  // open: eq
  // AND_Gate and_36 has open pins: in0=undriven, in1=comparator_97_gt, out=open
  Multiplexer #(.enable("false")) multiplexer_44 (
    .in0(undriven_2), .in1(1'b0), .out(multiplexer_44_out), .sel(comparator_97_lt));
  Multiplexer #(.width(3), .enable("false")) multiplexer_45 (
    .in0(multiplexer_43_out), .in1(3'b001), .out(MemRW), .sel(Inst_ID[5]));
  Comparator #(.width(6), .mode("unsigned")) comparator_98 (.a(Inst_ID), .b(6'b011100), .gt(BrUn));  // open: eq, lt

  // Other names for the same wires on the sheet: opcode[6:0] = Inst[6:0]; funct3[2:0] = Inst[14:12];
  //   funct7[6:0] = Inst[31:25]

  // Notes on the sheet:
  //   add
  //   mul
  //   sub
  //   sll
  //   mulh
  //   mulhu
  //   xor
  //   div
  //   divu
  //   srl
  //   or
  //   remu
  //   and
  //   xori
  //   andi
  //   lb
  //   lh
  //   lw
  //   lbu
  //   lhu
  //   addi
  //   slli
  //   slti
  //   slli
  //   ori
  //   sw
  //   beq
  //   blt
  //   bltu
  //   bne
  //   bgeu
  //   auipc
  //   lui
  //   jal
  //   jalr
  //   000 = I
  //   001 = S
  //   010 = B
  //   011 = U
  //   100 = J
endmodule

module imm (
  input  [24:0] Inst31to7,
  input  [2:0] ImmSel,
  output [31:0] Imm
);

  wire [31:0] B_type, I_type, J_type, S_type, U_type;

  Multiplexer #(.select(3), .width(32), .enable("false")) multiplexer_1 (
    .in0(I_type), .in1(S_type), .in2(B_type), .in3(U_type), .in4(J_type), .out(Imm), .sel(ImmSel));  // open: in5, in6, in7
  assign I_type = {{21{Inst31to7[24]}}, Inst31to7[23:13]};  // Bit_Extender bit_extender_1
  assign S_type = {{21{Inst31to7[24]}}, {Inst31to7[23:18], Inst31to7[4:0]}};  // Bit_Extender bit_extender_2
  assign B_type = {{20{Inst31to7[24]}}, {Inst31to7[0], Inst31to7[23:18], Inst31to7[4:1], 1'b0}};  // Bit_Extender bit_extender_3
  assign U_type = {{1{Inst31to7[24]}}, {Inst31to7[23:5], {12{1'b0}}}};  // Bit_Extender bit_extender_4
  assign J_type = {{12{Inst31to7[24]}}, {Inst31to7[12:5], Inst31to7[13], Inst31to7[23:14], 1'b0}};  // Bit_Extender bit_extender_5

  // Other names for the same wires on the sheet: Inst_8_11[3:0] = Inst31to7[4:1]; Inst_7 = Inst31to7[0];
  //   Inst_21_24[3:0] = Inst31to7[17:14]; Inst_25_30[5:0] = Inst31to7[23:18]; Inst_20 = Inst31to7[13];
  //   Inst_12_19[7:0] = Inst31to7[12:5]; Inst_31 = Inst31to7[24]

  // Notes on the sheet:
  //   spliter
  //   use 0-4 to match ISBUJ
  //   INPUT
  //   OUTPUT
  //   000 = I
  //   001 = S
  //   010 = B
  //   011 = U
  //   100 = J
  //   I type
  //   S_type
  //   B_type
  //   U_type
  //   J_type
endmodule

module branch (
  input  [31:0] DataA,
  input  [31:0] DataB,
  output BrEq,
  output BrLT
);

  Comparator #(.width(32)) comparator_1 (.a(DataA), .b(DataB), .eq(BrEq), .lt(BrLT));  // open: gt
endmodule
