// Logisim project mem.circ as structural Verilog: 1 circuit, main circuit main
module main (
  input  [31:0] WriteAddr,
  input  [31:0] WriteData,
  input  [2:0] MemRW,
  input  clk,
  output [31:0] ReadData
);

  wire sw;
  wire [7:0] lb;
  wire [15:8] lh;
  wire [31:0] bit_extender_1_out, bit_extender_2_out, bit_extender_3_out, bit_extender_4_out;
  wire [31:16] word_read_32b;

  Comparator #(.width(3)) comparator_1 (.a(MemRW), .b(3'b000), .eq(sw));  // open: gt, lt
  RAM #(.addrWidth(24), .dataWidth(32), .trigger("falling"), .databus("bibus")) ram_1 (
    .addr(WriteAddr[23:0]), .we(sw), .oe(1'b1), .clk(clk), .din(WriteData), .dout({word_read_32b, lh, lb}));
  assign bit_extender_1_out = {{24{lb[7]}}, lb};  // Bit_Extender bit_extender_1
  assign bit_extender_2_out = {{16{lh[15]}}, {lh, lb}};  // Bit_Extender bit_extender_2
  assign bit_extender_3_out = {{24{1'b0}}, lb};  // Bit_Extender bit_extender_3
  assign bit_extender_4_out = {{16{1'b0}}, {lh, lb}};  // Bit_Extender bit_extender_4
  Multiplexer #(.select(3), .width(32), .enable("false")) multiplexer_1 (
    .in1({word_read_32b, lh, lb}), .in2(bit_extender_1_out), .in3(bit_extender_2_out),
    .in4(bit_extender_3_out), .in5(bit_extender_4_out), .out(ReadData), .sel(MemRW));  // open: in0, in6, in7

  // Other names for the same wires on the sheet: lbu[7:0] = lb; lh[7:0] = lb; lhu[15:0] = {lh, lb};
  //   word_read_32b[15:0] = {lh, lb}

  // Notes on the sheet:
  //   INPUTS to your circuit
  //   0 = write
  //   1 = read
  //   2 = lb
  //   3 = lh
  //   4 = lbu
  //   5 = lhu
  //   OUTPUT from your circuit
endmodule
